// Digital circuit mips_bancodeRegistradores.dig as structural Verilog
module mips_bancodeRegistradores (
  input  Sinal_de_Escrita,
  input  [31:0] Escreve_Dado,
  input  [4:0] Escreve_Reg,
  input  [4:0] \Lê_Reg__de_Leitura_1 ,
  input  [4:0] \Lê_Reg__de_Leitura_2 ,
  output [31:0] \Lê_Dado_1 ,
  output [31:0] \Lê_Dado_2 
);

  wire and_1_out, and_2_out, and_3_out, and_4_out, and_5_out, and_6_out, and_7_out, and_8_out, and_9_out,
       and_10_out, and_11_out, and_12_out, and_13_out, and_14_out, and_15_out, and_16_out, and_17_out,
       and_18_out, and_19_out, and_20_out, and_21_out, and_22_out, and_23_out, and_24_out, and_25_out,
       and_26_out, and_27_out, and_28_out, and_29_out, and_30_out, and_31_out, and_32_out,
       mips_decodificador_1_p3, mips_decodificador_1_p4, mips_decodificador_1_p5, mips_decodificador_1_p6,
       mips_decodificador_1_p7, mips_decodificador_1_p8, mips_decodificador_1_p9, mips_decodificador_1_p10,
       mips_decodificador_1_p11, mips_decodificador_1_p12, mips_decodificador_1_p13,
       mips_decodificador_1_p14, mips_decodificador_1_p15, mips_decodificador_1_p16,
       mips_decodificador_1_p17, mips_decodificador_1_p18, mips_decodificador_1_p19,
       mips_decodificador_1_p20, mips_decodificador_1_p21, mips_decodificador_1_p22,
       mips_decodificador_1_p23, mips_decodificador_1_p24, mips_decodificador_1_p25,
       mips_decodificador_1_p26, mips_decodificador_1_p27, mips_decodificador_1_p28,
       mips_decodificador_1_p29, mips_decodificador_1_p30, undriven, undriven_2, undriven_3, undriven_4;
  wire [31:0] mips_reg32bits_1_saida, mips_reg32bits_2_saida, mips_reg32bits_3_saida, mips_reg32bits_4_saida,
       mips_reg32bits_5_saida, mips_reg32bits_6_saida, mips_reg32bits_7_saida, mips_reg32bits_8_saida,
       mips_reg32bits_9_saida, mips_reg32bits_10_saida, mips_reg32bits_11_saida, mips_reg32bits_12_saida,
       mips_reg32bits_13_saida, mips_reg32bits_14_saida, mips_reg32bits_15_saida, mips_reg32bits_16_saida,
       mips_reg32bits_17_saida, mips_reg32bits_18_saida, mips_reg32bits_19_saida, mips_reg32bits_20_saida,
       mips_reg32bits_21_saida, mips_reg32bits_22_saida, mips_reg32bits_23_saida, mips_reg32bits_24_saida,
       mips_reg32bits_25_saida, mips_reg32bits_26_saida, mips_reg32bits_27_saida, mips_reg32bits_28_saida,
       mips_reg32bits_29_saida, mips_reg32bits_30_saida, mips_reg32bits_31_saida, mips_reg32bits_32_saida;

  // mips_decodificador mips_decodificador_1: pin names not known; wires that end beside it: Escreve_Reg, Sinal_de_Escrita, mips_decodificador_1_p3, mips_decodificador_1_p4, mips_decodificador_1_p5, mips_decodificador_1_p6, mips_decodificador_1_p7, mips_decodificador_1_p8, mips_decodificador_1_p9, mips_decodificador_1_p10, mips_decodificador_1_p11, mips_decodificador_1_p12, mips_decodificador_1_p13, mips_decodificador_1_p14, mips_decodificador_1_p15, mips_decodificador_1_p16, mips_decodificador_1_p17, mips_decodificador_1_p18, mips_decodificador_1_p19, mips_decodificador_1_p20, mips_decodificador_1_p21, mips_decodificador_1_p22, mips_decodificador_1_p23, mips_decodificador_1_p24, mips_decodificador_1_p25, mips_decodificador_1_p26, mips_decodificador_1_p27, mips_decodificador_1_p28, mips_decodificador_1_p29, mips_decodificador_1_p30
  and and_1 (and_1_out, Sinal_de_Escrita, mips_decodificador_1_p3);
  and and_2 (and_2_out, Sinal_de_Escrita, mips_decodificador_1_p4);
  and and_3 (and_3_out, Sinal_de_Escrita, mips_decodificador_1_p5);
  and and_4 (and_4_out, Sinal_de_Escrita, mips_decodificador_1_p6);
  and and_5 (and_5_out, Sinal_de_Escrita, mips_decodificador_1_p7);
  and and_6 (and_6_out, Sinal_de_Escrita, mips_decodificador_1_p8);
  and and_7 (and_7_out, Sinal_de_Escrita, mips_decodificador_1_p9);
  and and_8 (and_8_out, Sinal_de_Escrita, mips_decodificador_1_p10);
  and and_9 (and_9_out, Sinal_de_Escrita, mips_decodificador_1_p11);
  and and_10 (and_10_out, Sinal_de_Escrita, mips_decodificador_1_p12);
  and and_11 (and_11_out, Sinal_de_Escrita, mips_decodificador_1_p13);
  and and_12 (and_12_out, Sinal_de_Escrita, mips_decodificador_1_p14);
  and and_13 (and_13_out, Sinal_de_Escrita, mips_decodificador_1_p15);
  and and_14 (and_14_out, Sinal_de_Escrita, mips_decodificador_1_p16);
  and and_15 (and_15_out, Sinal_de_Escrita, mips_decodificador_1_p17);
  and and_16 (and_16_out, Sinal_de_Escrita, mips_decodificador_1_p18);
  and and_17 (and_17_out, Sinal_de_Escrita, mips_decodificador_1_p19);
  and and_18 (and_18_out, Sinal_de_Escrita, mips_decodificador_1_p20);
  and and_19 (and_19_out, Sinal_de_Escrita, mips_decodificador_1_p21);
  and and_20 (and_20_out, Sinal_de_Escrita, mips_decodificador_1_p22);
  and and_21 (and_21_out, Sinal_de_Escrita, mips_decodificador_1_p23);
  and and_22 (and_22_out, Sinal_de_Escrita, mips_decodificador_1_p24);
  and and_23 (and_23_out, Sinal_de_Escrita, mips_decodificador_1_p25);
  and and_24 (and_24_out, Sinal_de_Escrita, mips_decodificador_1_p26);
  and and_25 (and_25_out, Sinal_de_Escrita, mips_decodificador_1_p27);
  and and_26 (and_26_out, Sinal_de_Escrita, mips_decodificador_1_p28);
  and and_27 (and_27_out, Sinal_de_Escrita, mips_decodificador_1_p29);
  and and_28 (and_28_out, Sinal_de_Escrita, mips_decodificador_1_p30);
  and and_29 (and_29_out, Sinal_de_Escrita, undriven);
  and and_30 (and_30_out, Sinal_de_Escrita, undriven_2);
  and and_31 (and_31_out, Sinal_de_Escrita, undriven_3);
  and and_32 (and_32_out, Sinal_de_Escrita, undriven_4);
  mips_reg32bits mips_reg32bits_1 (.Entrada(Escreve_Dado), .Clock(and_1_out), .Saida(mips_reg32bits_1_saida));
  mips_reg32bits mips_reg32bits_2 (.Entrada(Escreve_Dado), .Clock(and_2_out), .Saida(mips_reg32bits_2_saida));
  mips_reg32bits mips_reg32bits_3 (.Entrada(Escreve_Dado), .Clock(and_3_out), .Saida(mips_reg32bits_3_saida));
  mips_reg32bits mips_reg32bits_4 (.Entrada(Escreve_Dado), .Clock(and_4_out), .Saida(mips_reg32bits_4_saida));
  mips_reg32bits mips_reg32bits_5 (.Entrada(Escreve_Dado), .Clock(and_5_out), .Saida(mips_reg32bits_5_saida));
  mips_reg32bits mips_reg32bits_6 (.Entrada(Escreve_Dado), .Clock(and_6_out), .Saida(mips_reg32bits_6_saida));
  mips_reg32bits mips_reg32bits_7 (.Entrada(Escreve_Dado), .Clock(and_7_out), .Saida(mips_reg32bits_7_saida));
  mips_reg32bits mips_reg32bits_8 (.Entrada(Escreve_Dado), .Clock(and_8_out), .Saida(mips_reg32bits_8_saida));
  mips_reg32bits mips_reg32bits_9 (.Entrada(Escreve_Dado), .Clock(and_9_out), .Saida(mips_reg32bits_9_saida));
  mips_reg32bits mips_reg32bits_10 (.Entrada(Escreve_Dado), .Clock(and_10_out), .Saida(mips_reg32bits_10_saida));
  mips_reg32bits mips_reg32bits_11 (.Entrada(Escreve_Dado), .Clock(and_11_out), .Saida(mips_reg32bits_11_saida));
  mips_reg32bits mips_reg32bits_12 (.Entrada(Escreve_Dado), .Clock(and_12_out), .Saida(mips_reg32bits_12_saida));
  mips_reg32bits mips_reg32bits_13 (.Entrada(Escreve_Dado), .Clock(and_13_out), .Saida(mips_reg32bits_13_saida));
  mips_reg32bits mips_reg32bits_14 (.Entrada(Escreve_Dado), .Clock(and_14_out), .Saida(mips_reg32bits_14_saida));
  mips_reg32bits mips_reg32bits_15 (.Entrada(Escreve_Dado), .Clock(and_15_out), .Saida(mips_reg32bits_15_saida));
  mips_reg32bits mips_reg32bits_16 (.Entrada(Escreve_Dado), .Clock(and_16_out), .Saida(mips_reg32bits_16_saida));
  mips_reg32bits mips_reg32bits_17 (.Entrada(Escreve_Dado), .Clock(and_17_out), .Saida(mips_reg32bits_17_saida));
  mips_reg32bits mips_reg32bits_18 (.Entrada(Escreve_Dado), .Clock(and_18_out), .Saida(mips_reg32bits_18_saida));
  mips_reg32bits mips_reg32bits_19 (.Entrada(Escreve_Dado), .Clock(and_19_out), .Saida(mips_reg32bits_19_saida));
  mips_reg32bits mips_reg32bits_20 (.Entrada(Escreve_Dado), .Clock(and_20_out), .Saida(mips_reg32bits_20_saida));
  mips_reg32bits mips_reg32bits_21 (.Entrada(Escreve_Dado), .Clock(and_21_out), .Saida(mips_reg32bits_21_saida));
  mips_reg32bits mips_reg32bits_22 (.Entrada(Escreve_Dado), .Clock(and_22_out), .Saida(mips_reg32bits_22_saida));
  mips_reg32bits mips_reg32bits_23 (.Entrada(Escreve_Dado), .Clock(and_23_out), .Saida(mips_reg32bits_23_saida));
  mips_reg32bits mips_reg32bits_24 (.Entrada(Escreve_Dado), .Clock(and_24_out), .Saida(mips_reg32bits_24_saida));
  mips_reg32bits mips_reg32bits_25 (.Entrada(Escreve_Dado), .Clock(and_25_out), .Saida(mips_reg32bits_25_saida));
  mips_reg32bits mips_reg32bits_26 (.Entrada(Escreve_Dado), .Clock(and_26_out), .Saida(mips_reg32bits_26_saida));
  mips_reg32bits mips_reg32bits_27 (.Entrada(Escreve_Dado), .Clock(and_27_out), .Saida(mips_reg32bits_27_saida));
  mips_reg32bits mips_reg32bits_28 (.Entrada(Escreve_Dado), .Clock(and_28_out), .Saida(mips_reg32bits_28_saida));
  mips_reg32bits mips_reg32bits_29 (.Entrada(Escreve_Dado), .Clock(and_29_out), .Saida(mips_reg32bits_29_saida));
  mips_reg32bits mips_reg32bits_30 (.Entrada(Escreve_Dado), .Clock(and_30_out), .Saida(mips_reg32bits_30_saida));
  mips_reg32bits mips_reg32bits_31 (.Entrada(Escreve_Dado), .Clock(and_31_out), .Saida(mips_reg32bits_31_saida));
  mips_reg32bits mips_reg32bits_32 (.Entrada(Escreve_Dado), .Clock(and_32_out), .Saida(mips_reg32bits_32_saida));
  mips_mux32 mips_mux32_1 (
    .Entrada0(mips_reg32bits_1_saida), .Entrada1(mips_reg32bits_2_saida), .Entrada2(mips_reg32bits_3_saida),
    .Entrada3(mips_reg32bits_4_saida), .Entrada4(mips_reg32bits_5_saida), .Entrada5(mips_reg32bits_6_saida),
    .Entrada6(mips_reg32bits_7_saida), .Entrada7(mips_reg32bits_8_saida), .Entrada8(mips_reg32bits_9_saida),
    .Entrada9(mips_reg32bits_10_saida), .Entrada10(mips_reg32bits_11_saida),
    .Entrada11(mips_reg32bits_12_saida), .Entrada12(mips_reg32bits_13_saida),
    .Entrada13(mips_reg32bits_14_saida), .Entrada14(mips_reg32bits_15_saida),
    .Entrada15(mips_reg32bits_16_saida), .Entrada16(mips_reg32bits_17_saida),
    .Entrada17(mips_reg32bits_18_saida), .Entrada18(mips_reg32bits_19_saida),
    .Entrada19(mips_reg32bits_20_saida), .Entrada20(mips_reg32bits_21_saida),
    .Entrada21(mips_reg32bits_22_saida), .Entrada22(mips_reg32bits_23_saida),
    .Entrada23(mips_reg32bits_24_saida), .Entrada24(mips_reg32bits_25_saida),
    .Entrada25(mips_reg32bits_26_saida), .Entrada26(mips_reg32bits_27_saida),
    .Entrada27(mips_reg32bits_28_saida), .Entrada28(mips_reg32bits_29_saida),
    .Entrada29(mips_reg32bits_30_saida), .Entrada30(mips_reg32bits_31_saida),
    .Entrada31(mips_reg32bits_32_saida), .\Seleção (\Lê_Reg__de_Leitura_1 ), .Saida(\Lê_Dado_1 ));
  mips_mux32 mips_mux32_2 (
    .Entrada0(mips_reg32bits_1_saida), .Entrada1(mips_reg32bits_2_saida), .Entrada2(mips_reg32bits_3_saida),
    .Entrada3(mips_reg32bits_4_saida), .Entrada4(mips_reg32bits_5_saida), .Entrada5(mips_reg32bits_6_saida),
    .Entrada6(mips_reg32bits_7_saida), .Entrada7(mips_reg32bits_8_saida), .Entrada8(mips_reg32bits_9_saida),
    .Entrada9(mips_reg32bits_10_saida), .Entrada10(mips_reg32bits_11_saida),
    .Entrada11(mips_reg32bits_12_saida), .Entrada12(mips_reg32bits_13_saida),
    .Entrada13(mips_reg32bits_14_saida), .Entrada14(mips_reg32bits_15_saida),
    .Entrada15(mips_reg32bits_16_saida), .Entrada16(mips_reg32bits_17_saida),
    .Entrada17(mips_reg32bits_18_saida), .Entrada18(mips_reg32bits_19_saida),
    .Entrada19(mips_reg32bits_20_saida), .Entrada20(mips_reg32bits_21_saida),
    .Entrada21(mips_reg32bits_22_saida), .Entrada22(mips_reg32bits_23_saida),
    .Entrada23(mips_reg32bits_24_saida), .Entrada24(mips_reg32bits_25_saida),
    .Entrada25(mips_reg32bits_26_saida), .Entrada26(mips_reg32bits_27_saida),
    .Entrada27(mips_reg32bits_28_saida), .Entrada28(mips_reg32bits_29_saida),
    .Entrada29(mips_reg32bits_30_saida), .Entrada30(mips_reg32bits_31_saida),
    .Entrada31(mips_reg32bits_32_saida), .\Seleção (\Lê_Reg__de_Leitura_2 ), .Saida(\Lê_Dado_2 ));
  // Pins of 1 and 32 bits meet at \Lê_Dado_2 
endmodule
