// Digital circuit mips_mux4de32bits.dig as structural Verilog
module mips_mux4de32bits (
  input  [31:0] Entrada0,
  input  [31:0] Entrada1,
  input  [31:0] Entrada2,
  input  [31:0] Entrada3,
  input  \Seleção0 ,
  input  \Seleção1 ,
  output [31:0] Saida
);

  wire mips_mux2_1_p4, mips_mux2_2_p4;

  // mips_mux2 mips_mux2_1: pin names not known; wires that end beside it: Entrada0, Entrada1, \Seleção0 , mips_mux2_1_p4, Saida
  // mips_mux2 mips_mux2_2: pin names not known; wires that end beside it: Entrada2, Entrada3, \Seleção0 , mips_mux2_2_p4
  mips_mux2 mips_mux2_3 (.Entrada0(mips_mux2_1_p4), .Entrada1(mips_mux2_2_p4), .\Seleção (\Seleção1 ));  // open: Saida
endmodule
