// Digital circuit ULA16BITS_TESTE.dig as structural Verilog
module ULA16BITS_TESTE (
  input  Binvert,
  input  Ainvert,
  input  CarryIn,
  input  [1:0] \Operação ,
  input  Less,
  input  [15:0] A,
  input  [15:0] B,
  output Saida0,
  output Saida1,
  output Saida2,
  output Saida3,
  output Saida4,
  output Saida5,
  output Saida6,
  output Saida7,
  output Saida8,
  output Saida9,
  output Saida10,
  output Saida11,
  output Saida12,
  output Saida13,
  output Saida14,
  output Saida15,
  output CarryOut,
  output Set
);

  wire mips_ula1bit_set_1_carryout, mips_ula1bit_set_2_carryout, mips_ula1bit_set_3_carryout,
       mips_ula1bit_set_4_carryout, mips_ula1bit_set_5_carryout, mips_ula1bit_set_6_carryout,
       mips_ula1bit_set_7_carryout, mips_ula1bit_set_8_carryout, mips_ula1bit_set_9_carryout,
       mips_ula1bit_set_10_carryout, mips_ula1bit_set_11_carryout, mips_ula1bit_set_12_carryout,
       mips_ula1bit_set_13_carryout, mips_ula1bit_set_14_carryout, mips_ula1bit_set_15_carryout;

  mips_ULA1bit_set mips_ula1bit_set_1 (
    .A(A[0]), .B(B[0]), .CarryIn(CarryIn), .Less(Less), .Ainvert(Ainvert), .Binvert(Binvert),
    .\Operação (\Operação ), .CarryOut(mips_ula1bit_set_1_carryout), .Resultado(Saida0));  // open: Set
  mips_ULA1bit_set mips_ula1bit_set_2 (
    .A(A[1]), .B(B[1]), .CarryIn(mips_ula1bit_set_1_carryout), .Less(1'b0), .Ainvert(Ainvert),
    .Binvert(Binvert), .\Operação (\Operação ), .CarryOut(mips_ula1bit_set_2_carryout), .Resultado(Saida1));  // open: Set
  mips_ULA1bit_set mips_ula1bit_set_3 (
    .A(A[2]), .B(B[2]), .CarryIn(mips_ula1bit_set_2_carryout), .Less(1'b0), .Ainvert(Ainvert),
    .Binvert(Binvert), .\Operação (\Operação ), .CarryOut(mips_ula1bit_set_3_carryout), .Resultado(Saida2));  // open: Set
  mips_ULA1bit_set mips_ula1bit_set_4 (
    .A(A[3]), .B(B[3]), .CarryIn(mips_ula1bit_set_3_carryout), .Less(1'b0), .Ainvert(Ainvert),
    .Binvert(Binvert), .\Operação (\Operação ), .CarryOut(mips_ula1bit_set_4_carryout), .Resultado(Saida3));  // open: Set
  mips_ULA1bit_set mips_ula1bit_set_5 (
    .A(A[4]), .B(B[4]), .CarryIn(mips_ula1bit_set_4_carryout), .Less(1'b0), .Ainvert(Ainvert),
    .Binvert(Binvert), .\Operação (\Operação ), .CarryOut(mips_ula1bit_set_5_carryout), .Resultado(Saida4));  // open: Set
  mips_ULA1bit_set mips_ula1bit_set_6 (
    .A(A[5]), .B(B[5]), .CarryIn(mips_ula1bit_set_5_carryout), .Less(1'b0), .Ainvert(Ainvert),
    .Binvert(Binvert), .\Operação (\Operação ), .CarryOut(mips_ula1bit_set_6_carryout), .Resultado(Saida5));  // open: Set
  mips_ULA1bit_set mips_ula1bit_set_7 (
    .A(A[6]), .B(B[6]), .CarryIn(mips_ula1bit_set_6_carryout), .Less(1'b0), .Ainvert(Ainvert),
    .Binvert(Binvert), .\Operação (\Operação ), .CarryOut(mips_ula1bit_set_7_carryout), .Resultado(Saida6));  // open: Set
  mips_ULA1bit_set mips_ula1bit_set_8 (
    .A(A[7]), .B(B[7]), .CarryIn(mips_ula1bit_set_7_carryout), .Less(1'b0), .Ainvert(Ainvert),
    .Binvert(Binvert), .\Operação (\Operação ), .CarryOut(mips_ula1bit_set_8_carryout), .Resultado(Saida7));  // open: Set
  mips_ULA1bit_set mips_ula1bit_set_9 (
    .A(A[8]), .B(B[8]), .CarryIn(mips_ula1bit_set_8_carryout), .Less(1'b0), .Ainvert(Ainvert),
    .Binvert(Binvert), .\Operação (\Operação ), .CarryOut(mips_ula1bit_set_9_carryout), .Resultado(Saida8));  // open: Set
  mips_ULA1bit_set mips_ula1bit_set_10 (
    .A(A[9]), .B(B[9]), .CarryIn(mips_ula1bit_set_9_carryout), .Less(1'b0), .Ainvert(Ainvert),
    .Binvert(Binvert), .\Operação (\Operação ), .CarryOut(mips_ula1bit_set_10_carryout), .Resultado(Saida9));  // open: Set
  mips_ULA1bit_set mips_ula1bit_set_11 (
    .A(A[10]), .B(B[10]), .CarryIn(mips_ula1bit_set_10_carryout), .Less(1'b0), .Ainvert(Ainvert),
    .Binvert(Binvert), .\Operação (\Operação ), .CarryOut(mips_ula1bit_set_11_carryout), .Resultado(Saida10));  // open: Set
  mips_ULA1bit_set mips_ula1bit_set_12 (
    .A(A[11]), .B(B[11]), .CarryIn(mips_ula1bit_set_11_carryout), .Less(1'b0), .Ainvert(Ainvert),
    .Binvert(Binvert), .\Operação (\Operação ), .CarryOut(mips_ula1bit_set_12_carryout), .Resultado(Saida11));  // open: Set
  mips_ULA1bit_set mips_ula1bit_set_13 (
    .A(A[12]), .B(B[12]), .CarryIn(mips_ula1bit_set_12_carryout), .Less(1'b0), .Ainvert(Ainvert),
    .Binvert(Binvert), .\Operação (\Operação ), .CarryOut(mips_ula1bit_set_13_carryout), .Resultado(Saida12));  // open: Set
  mips_ULA1bit_set mips_ula1bit_set_14 (
    .A(A[13]), .B(B[13]), .CarryIn(mips_ula1bit_set_13_carryout), .Less(1'b0), .Ainvert(Ainvert),
    .Binvert(Binvert), .\Operação (\Operação ), .CarryOut(mips_ula1bit_set_14_carryout), .Resultado(Saida13));  // open: Set
  mips_ULA1bit_set mips_ula1bit_set_15 (
    .A(A[14]), .B(B[14]), .CarryIn(mips_ula1bit_set_14_carryout), .Less(1'b0), .Ainvert(Ainvert),
    .Binvert(Binvert), .\Operação (\Operação ), .CarryOut(mips_ula1bit_set_15_carryout), .Resultado(Saida14));  // open: Set
  mips_ULA1bit_set mips_ula1bit_set_16 (
    .A(A[15]), .B(B[15]), .CarryIn(mips_ula1bit_set_15_carryout), .Less(1'b0), .Ainvert(Ainvert),
    .Binvert(Binvert), .\Operação (\Operação ), .CarryOut(CarryOut), .Resultado(Saida15), .Set(Set));
endmodule
