// Digital circuit mips_Controle.dig as structural Verilog
module mips_Controle (
  input  [5:0] Entradas,
  input  Clock,
  input  Sinal,
  output RegDst,
  output ALU_Scr,
  output MemToReg,
  output RegWrite,
  output MemRead,
  output MemWrite,
  output Branch,
  output ALUop_1,
  output ALUop_0,
  output Jump,
  output AtuaPC,
  output BNE
);

  wire and_1_out, and_2_out, and_3_out, and_4_out, and_5_out, and_8_out, and_9_out, nand_1_out, or_1_out,
       or_2_out, or_3_out, or_4_out;
  wire [1:0] mips_flipflopd_1_p2;

  and and_1 (and_1_out, ~Entradas[5], ~Entradas[4], Entradas[3], ~Entradas[2], ~Entradas[1], ~Entradas[0]);  // And
  and and_2 (and_2_out, ~Entradas[5], ~Entradas[4], ~Entradas[3], ~Entradas[2], ~Entradas[1], ~Entradas[0]);  // And
  and and_3 (and_3_out, Entradas[5], ~Entradas[4], ~Entradas[3], ~Entradas[2], Entradas[1], Entradas[0]);  // And
  and and_4 (and_4_out, Entradas[5], ~Entradas[4], Entradas[3], ~Entradas[2], Entradas[1], Entradas[0]);  // And
  and and_5 (and_5_out, ~Entradas[5], ~Entradas[4], ~Entradas[3], Entradas[2], ~Entradas[1], ~Entradas[0]);  // And
  and and_6 (Jump, ~Entradas[5], ~Entradas[4], ~Entradas[3], ~Entradas[2], Entradas[1], ~Entradas[0]);  // And
  and and_7 (BNE, ~Entradas[5], ~Entradas[4], ~Entradas[3], Entradas[2], ~Entradas[1], Entradas[0]);  // And
  and and_8 (and_8_out, Entradas[5], Entradas[4], Entradas[3], Entradas[2], Entradas[1], Entradas[0]);
  or or_1 (or_1_out, and_5_out, BNE);
  and and_9 (and_9_out, ~and_8_out, Clock, Sinal);  // And
  // mips_flipflopD mips_flipflopd_1: pin names not known; wires that end beside it: and_9_out, mips_flipflopd_1_p2
  or or_2 (or_2_out, and_3_out, and_1_out, and_4_out);
  or or_3 (or_3_out, and_1_out, and_2_out, and_3_out);
  or or_4 (or_4_out, mips_flipflopd_1_p2[0], mips_flipflopd_1_p2[1]);
  nand nand_1 (nand_1_out, mips_flipflopd_1_p2[0], ~mips_flipflopd_1_p2[1]);  // NAnd
  not not_1 (AtuaPC, or_4_out);
  and and_10 (RegDst, ~Jump, or_4_out, and_2_out);  // And
  and and_11 (ALU_Scr, ~Jump, or_4_out, or_2_out);  // And
  and and_12 (MemToReg, ~Jump, or_4_out, and_3_out);  // And
  and and_13 (MemRead, ~Jump, or_4_out, and_3_out);  // And
  and and_14 (MemWrite, ~Jump, or_4_out, and_4_out);  // And
  and and_15 (Branch, ~Jump, or_4_out, or_1_out);  // And
  and and_16 (ALUop_1, ~Jump, or_4_out, and_2_out);  // And
  and and_17 (ALUop_0, ~Jump, or_4_out, or_1_out);  // And
  and and_18 (RegWrite, ~Jump, or_4_out, or_3_out, nand_1_out);  // And
endmodule
