// Digital circuit mips_Controle_Milene(jump e addi).dig as structural Verilog
module mips_Controle_Milene_jump_e_addi (
  input  Op0,
  input  Op1,
  input  Op2,
  input  Op3,
  input  Op4,
  input  Op5,
  output RegDst,
  output OrigALU,
  output MemParaReg,
  output EscreveReg,
  output LeMem,
  output EscreveMem,
  output Branch,
  output ALUOp0,
  output ALUOp1,
  output addi,
  output jump
);

  wire and_1_out, and_2_out, not_1_out, not_2_out, not_3_out, not_4_out, not_5_out;

  not not_1 (not_1_out, Op0);
  not not_2 (not_2_out, Op1);
  not not_3 (not_3_out, Op2);
  not not_4 (not_4_out, Op3);
  not not_5 (not_5_out, Op4);
  not not_6 (RegDst, Op5);
  and and_1 (and_1_out, not_1_out, not_2_out, not_3_out, not_4_out, not_5_out, RegDst);
  and and_2 (and_2_out, Op0, not_2_out, not_3_out, not_4_out, Op4, Op5);
  and and_3 (LeMem, Op0, not_2_out, not_3_out, not_4_out, Op4, Op5);
  and and_4 (EscreveMem, Op0, not_2_out, Op2, not_4_out, Op4, Op5);
  and and_5 (ALUOp0, not_4_out, RegDst);
  and and_6 (addi, not_1_out, not_2_out, Op2, not_4_out, not_5_out, RegDst);
  and and_7 (jump, not_1_out, not_2_out, not_3_out, not_4_out, Op4, RegDst);
  or or_1 (EscreveReg, and_1_out, and_2_out);

  assign ALUOp1 = Op3;
  assign Branch = Op3;
  assign MemParaReg = Op5;
  assign OrigALU = Op5;
endmodule
