// Digital circuit mips_Controle_Milene.dig as structural Verilog
module mips_Controle_Milene (
  input  Op2,
  input  Op3,
  input  Op5,
  output RegDst,
  output OrigALU,
  output MemParaReg,
  output EscreveReg,
  output LeMem,
  output EscreveMem,
  output Branch,
  output ALUOp0,
  output ALUOp1
);

  wire not_1_out, not_2_out;

  not not_1 (not_1_out, Op2);
  not not_2 (not_2_out, Op3);
  not not_3 (RegDst, Op5);
  and and_1 (EscreveReg, not_1_out, not_2_out);
  and and_2 (LeMem, not_1_out, Op5);
  and and_3 (ALUOp0, not_2_out, RegDst);

  assign ALUOp1 = Op3;
  assign Branch = Op3;
  assign EscreveMem = Op2;
  assign MemParaReg = Op5;
  assign OrigALU = Op5;
endmodule
