// Digital circuit mips_ULA16bits.dig as structural Verilog
module mips_ULA16bits (
  input  Ainvert,
  input  Binvert,
  input  [1:0] \Operação ,
  input  CarryIn,
  input  [15:0] A,
  input  [15:0] B,
  output Result0,
  output Result1,
  output Result2,
  output Result3,
  output Result4,
  output Result5,
  output Result6,
  output Result7,
  output Result8,
  output Result9,
  output Result10,
  output Result11,
  output Result12,
  output Result13,
  output Result14,
  output Result15
);

  wire mips_ula8bits_aberta_1_carryout, mips_ula8bits_aberta_2_carryout;

  mips_ULA8bits_aberta mips_ula8bits_aberta_1 (
    .Ainvert(Ainvert), .Binvert(Binvert), .CarryIn(CarryIn), .\Operação (\Operação ), .A(A[7:0]), .B(B[7:0]),
    .Less(mips_ula8bits_aberta_2_carryout), .CarryOut(mips_ula8bits_aberta_1_carryout), .Result0(Result0),
    .Result1(Result1), .Result2(Result2), .Result3(Result3), .Result4(Result4), .Result5(Result5),
    .Result6(Result6), .Result7(Result7));
  mips_ULA8bits_aberta mips_ula8bits_aberta_2 (
    .Ainvert(Ainvert), .Binvert(Binvert), .CarryIn(mips_ula8bits_aberta_1_carryout), .\Operação (\Operação ),
    .A(A[15:8]), .B(B[15:8]), .Less(1'b0), .CarryOut(mips_ula8bits_aberta_2_carryout), .Result0(Result8),
    .Result1(Result9), .Result2(Result10), .Result3(Result11), .Result4(Result12), .Result5(Result13),
    .Result6(Result14), .Result7(Result15));
endmodule

/* Test case:
	Operação	A	B	Ainvert		Binvert		CarryIn		Result15	Result14	Result13	Result12	Result11	Result10	Result9		Result8		Result7		Result6		Result5		Result4		Result3		Result2		Result1		Result0
loop(a,16)
	loop(b,16)
		0	(a)	(b)	0	0	0	bits(16,a&b)
		1	(a)	(b)	0	0	0	bits(16,a|b)
		10	(a)	(b)	0	0	0	bits(16,a+b)
		10	(a)	(b)	0	1	1	bits(16,a-b)
		0	(a)	(b)	1	1	0	bits(16,~(a|b))
	end loop
end loop
*/
