// Digital circuit mips_ULA16bits_aberta.dig as structural Verilog
module mips_ULA16bits_aberta (
  input  A0,
  input  B0,
  input  A1,
  input  B1,
  input  A2,
  input  B2,
  input  A3,
  input  B3,
  input  A4,
  input  B4,
  input  A5,
  input  B5,
  input  A6,
  input  B6,
  input  A7,
  input  B7,
  input  A8,
  input  B8,
  input  A9,
  input  B9,
  input  A10,
  input  B10,
  input  A11,
  input  B11,
  input  A12,
  input  B12,
  input  A13,
  input  B13,
  input  A14,
  input  B14,
  input  A15,
  input  B15,
  input  Ainvert,
  input  Binvert,
  input  \Operação ,
  input  Less,
  input  CarryIn,
  output Saida0,
  output Saida1,
  output Saida2,
  output Saida3,
  output Saida4,
  output Saida5,
  output Saida6,
  output Saida7,
  output Saida8,
  output Saida9,
  output Saida10,
  output Saida11,
  output Saida12,
  output Saida13,
  output Saida14,
  output Saida15,
  output CarryOut
);

  wire mips_ula8bits_aberta_1_carryout;

  mips_ULA8bits_aberta mips_ula8bits_aberta_1 (
    .A0(A0), .B0(B0), .A1(A1), .B1(B1), .A2(A2), .B2(B2), .A3(A3), .B3(B3), .A4(A4), .B4(B4), .A5(A5),
    .B5(B5), .A6(A6), .B6(B6), .A7(A7), .B7(B7), .Ainvert(Ainvert), .Binvert(Binvert), .CarryIn(CarryIn),
    .Less(Less), .\Operação (\Operação ), .Saida0(Saida0), .Saida1(Saida1), .Saida2(Saida2), .Saida3(Saida3),
    .Saida4(Saida4), .Saida5(Saida5), .Saida6(Saida6), .Saida7(Saida7),
    .CarryOut(mips_ula8bits_aberta_1_carryout));
  mips_ULA8bits_aberta mips_ula8bits_aberta_2 (
    .A0(A8), .B0(B8), .A1(A9), .B1(B9), .A2(A10), .B2(B10), .A3(A11), .B3(B11), .A4(A12), .B4(B12), .A5(A13),
    .B5(B13), .A6(A14), .B6(B14), .A7(A15), .B7(B15), .Ainvert(Ainvert), .Binvert(Binvert),
    .CarryIn(mips_ula8bits_aberta_1_carryout), .Less(1'b0), .\Operação (\Operação ), .Saida0(Saida8),
    .Saida1(Saida9), .Saida2(Saida10), .Saida3(Saida11), .Saida4(Saida12), .Saida5(Saida13),
    .Saida6(Saida14), .Saida7(Saida15), .CarryOut(CarryOut));
endmodule
