// Digital circuit mips_ULA1bit.dig as structural Verilog
module mips_ULA1bit (
  input  A,
  input  B,
  input  CarryIn,
  input  Less,
  input  Ainvert,
  input  Binvert,
  input  [1:0] \Operação ,
  output CarryOut,
  output Resultado
);

  wire and_1_out, mips_mux2_1_s_2, mips_mux2_2_s_2, mips_mux2_3_s_2, mips_mux2_4_s_2, mips_somacomplet_1_s,
       not_1_out, not_2_out, or_1_out;

  not not_1 (not_1_out, A);
  not not_2 (not_2_out, B);
  mips_mux2 mips_mux2_1 (.A(B), .B(not_2_out), .S(Binvert), .S_2(mips_mux2_1_s_2));
  mips_mux2 mips_mux2_2 (.A(A), .B(not_1_out), .S(Ainvert), .S_2(mips_mux2_2_s_2));
  and and_1 (and_1_out, mips_mux2_2_s_2, mips_mux2_1_s_2);
  or or_1 (or_1_out, mips_mux2_2_s_2, mips_mux2_1_s_2);
  mips_somacomplet mips_somacomplet_1 (
    .A(mips_mux2_2_s_2), .B(mips_mux2_1_s_2), .CarryIn(CarryIn), .S(mips_somacomplet_1_s), .CarryOut(CarryOut));
  mips_mux2 mips_mux2_3 (.A(and_1_out), .B(or_1_out), .S(\Operação [1]), .S_2(mips_mux2_3_s_2));
  mips_mux2 mips_mux2_4 (.A(mips_somacomplet_1_s), .B(Less), .S(\Operação [1]), .S_2(mips_mux2_4_s_2));
  mips_mux2 mips_mux2_5 (.A(mips_mux2_3_s_2), .B(mips_mux2_4_s_2), .S(\Operação [0]), .S_2(Resultado));
  // Pins of 1 and 2 bits meet at \Operação 
endmodule
