// Digital circuit mips_ULA1bit_set.dig as structural Verilog
module mips_ULA1bit_set (
  input  A,
  input  B,
  input  CarryIn,
  input  Less,
  input  Ainvert,
  input  Binvert,
  input  [1:0] \Operação ,
  output CarryOut,
  output Resultado,
  output Set
);

  wire and_1_out, mips_mux2_1_saida, mips_mux2_2_saida, not_1_out, not_2_out, or_1_out;

  not not_1 (not_1_out, A);
  not not_2 (not_2_out, B);
  mips_mux2 mips_mux2_1 (.Entrada0(A), .Entrada1(not_1_out), .\Seleção (Ainvert), .Saida(mips_mux2_1_saida));
  mips_mux2 mips_mux2_2 (.Entrada0(B), .Entrada1(not_2_out), .\Seleção (Binvert), .Saida(mips_mux2_2_saida));
  and and_1 (and_1_out, mips_mux2_1_saida, mips_mux2_2_saida);
  or or_1 (or_1_out, mips_mux2_1_saida, mips_mux2_2_saida);
  mips_somacomplet mips_somacomplet_1 (
    .A(mips_mux2_1_saida), .B(mips_mux2_2_saida), .CarryIn(CarryIn), .S(Set), .CarryOut(CarryOut));
  // mips_mux4 mips_mux4_1: pin names not known; wires that end beside it: and_1_out, Less, \Operação [0], \Operação [1], or_1_out, Set, Resultado
endmodule

/* Test case:
	Operação	A	B	Ainvert		Binvert		CarryIn		Less	Resultado
loop(a,2)
	loop(b,2)
		0	(a)	(b)	0	0	0	0	(a&b)
		1	(a)	(b)	0	0	0	0	(a|b)
	end loop
end loop
*/
