// Digital circuit mips_ULA32bits_aberta.dig as structural Verilog
module mips_ULA32bits_aberta (
);

  mips_ULA16bits_aberta mips_ula16bits_aberta_1 ();  // open: Ainvert, Binvert, Operação, CarryIn, A, B, Less, Saida0, Saida1, Saida2, Saida3, Saida4, Saida5, Saida6, Saida7, Saida8, Saida9, Saida10, Saida11, Saida12, Saida13, Saida14, Saida15, CarryOut
  mips_ULA16bits_aberta mips_ula16bits_aberta_2 ();  // open: Ainvert, Binvert, Operação, CarryIn, A, B, Less, Saida0, Saida1, Saida2, Saida3, Saida4, Saida5, Saida6, Saida7, Saida8, Saida9, Saida10, Saida11, Saida12, Saida13, Saida14, Saida15, CarryOut
endmodule
