// Digital circuit mips_ULA32bits_newmodel.dig as structural Verilog
module mips_ULA32bits_newmodel (
  input  Binvert,
  input  Ainvert,
  input  CarryIn,
  input  [1:0] \Operação ,
  input  [31:0] Entrada0,
  input  [31:0] Entrada1,
  output CarryOut,
  output [31:0] Saida
);

  wire mips_ula1bit_set_1_carryout, mips_ula1bit_set_2_carryout, mips_ula1bit_set_3_carryout,
       mips_ula1bit_set_4_carryout, mips_ula1bit_set_5_carryout, mips_ula1bit_set_6_carryout,
       mips_ula1bit_set_7_carryout, mips_ula1bit_set_8_carryout, mips_ula1bit_set_9_carryout,
       mips_ula1bit_set_10_carryout, mips_ula1bit_set_11_carryout, mips_ula1bit_set_12_carryout,
       mips_ula1bit_set_13_carryout, mips_ula1bit_set_14_carryout, mips_ula1bit_set_15_carryout,
       mips_ula1bit_set_16_carryout, mips_ula1bit_set_17_carryout, mips_ula1bit_set_18_carryout,
       mips_ula1bit_set_19_carryout, mips_ula1bit_set_20_carryout, mips_ula1bit_set_21_carryout,
       mips_ula1bit_set_22_carryout, mips_ula1bit_set_23_carryout, mips_ula1bit_set_24_carryout,
       mips_ula1bit_set_25_carryout, mips_ula1bit_set_26_carryout, mips_ula1bit_set_27_carryout,
       mips_ula1bit_set_28_carryout, mips_ula1bit_set_29_carryout, mips_ula1bit_set_30_carryout,
       mips_ula1bit_set_31_carryout, mips_ula1bit_set_32_set;

  mips_ULA1bit_set mips_ula1bit_set_1 (
    .A(Entrada0[0]), .B(Entrada1[0]), .CarryIn(CarryIn), .Less(mips_ula1bit_set_32_set), .Ainvert(Ainvert),
    .Binvert(Binvert), .CarryOut(mips_ula1bit_set_1_carryout), .Resultado(Saida[0]), .\Operação (\Operação ));  // open: Set
  mips_ULA1bit_set mips_ula1bit_set_2 (
    .A(Entrada0[1]), .B(Entrada1[1]), .CarryIn(mips_ula1bit_set_1_carryout), .Less(1'b0), .Ainvert(Ainvert),
    .Binvert(Binvert), .CarryOut(mips_ula1bit_set_2_carryout), .Resultado(Saida[1]), .\Operação (\Operação ));  // open: Set
  mips_ULA1bit_set mips_ula1bit_set_3 (
    .A(Entrada0[2]), .B(Entrada1[2]), .CarryIn(mips_ula1bit_set_2_carryout), .Less(1'b0), .Ainvert(Ainvert),
    .Binvert(Binvert), .CarryOut(mips_ula1bit_set_3_carryout), .Resultado(Saida[2]), .\Operação (\Operação ));  // open: Set
  mips_ULA1bit_set mips_ula1bit_set_4 (
    .A(Entrada0[3]), .B(Entrada1[3]), .CarryIn(mips_ula1bit_set_3_carryout), .Less(1'b0), .Ainvert(Ainvert),
    .Binvert(Binvert), .CarryOut(mips_ula1bit_set_4_carryout), .Resultado(Saida[3]), .\Operação (\Operação ));  // open: Set
  mips_ULA1bit_set mips_ula1bit_set_5 (
    .A(Entrada0[4]), .B(Entrada1[4]), .CarryIn(mips_ula1bit_set_4_carryout), .Less(1'b0), .Ainvert(Ainvert),
    .Binvert(Binvert), .CarryOut(mips_ula1bit_set_5_carryout), .Resultado(Saida[4]), .\Operação (\Operação ));  // open: Set
  mips_ULA1bit_set mips_ula1bit_set_6 (
    .A(Entrada0[5]), .B(Entrada1[5]), .CarryIn(mips_ula1bit_set_5_carryout), .Less(1'b0), .Ainvert(Ainvert),
    .Binvert(Binvert), .CarryOut(mips_ula1bit_set_6_carryout), .Resultado(Saida[5]), .\Operação (\Operação ));  // open: Set
  mips_ULA1bit_set mips_ula1bit_set_7 (
    .A(Entrada0[6]), .B(Entrada1[6]), .CarryIn(mips_ula1bit_set_6_carryout), .Less(1'b0), .Ainvert(Ainvert),
    .Binvert(Binvert), .CarryOut(mips_ula1bit_set_7_carryout), .Resultado(Saida[6]), .\Operação (\Operação ));  // open: Set
  mips_ULA1bit_set mips_ula1bit_set_8 (
    .A(Entrada0[7]), .B(Entrada1[7]), .CarryIn(mips_ula1bit_set_7_carryout), .Less(1'b0), .Ainvert(Ainvert),
    .Binvert(Binvert), .CarryOut(mips_ula1bit_set_8_carryout), .Resultado(Saida[7]), .\Operação (\Operação ));  // open: Set
  mips_ULA1bit_set mips_ula1bit_set_9 (
    .A(Entrada0[8]), .B(Entrada1[8]), .CarryIn(mips_ula1bit_set_8_carryout), .Less(1'b0), .Ainvert(Ainvert),
    .Binvert(Binvert), .CarryOut(mips_ula1bit_set_9_carryout), .Resultado(Saida[8]), .\Operação (\Operação ));  // open: Set
  mips_ULA1bit_set mips_ula1bit_set_10 (
    .A(Entrada0[9]), .B(Entrada1[9]), .CarryIn(mips_ula1bit_set_9_carryout), .Less(1'b0), .Ainvert(Ainvert),
    .Binvert(Binvert), .CarryOut(mips_ula1bit_set_10_carryout), .Resultado(Saida[9]), .\Operação (\Operação ));  // open: Set
  mips_ULA1bit_set mips_ula1bit_set_11 (
    .A(Entrada0[10]), .B(Entrada1[10]), .CarryIn(mips_ula1bit_set_10_carryout), .Less(1'b0),
    .Ainvert(Ainvert), .Binvert(Binvert), .CarryOut(mips_ula1bit_set_11_carryout), .Resultado(Saida[10]),
    .\Operação (\Operação ));  // open: Set
  mips_ULA1bit_set mips_ula1bit_set_12 (
    .A(Entrada0[11]), .B(Entrada1[11]), .CarryIn(mips_ula1bit_set_11_carryout), .Less(1'b0),
    .Ainvert(Ainvert), .Binvert(Binvert), .CarryOut(mips_ula1bit_set_12_carryout), .Resultado(Saida[11]),
    .\Operação (\Operação ));  // open: Set
  mips_ULA1bit_set mips_ula1bit_set_13 (
    .A(Entrada0[12]), .B(Entrada1[12]), .CarryIn(mips_ula1bit_set_12_carryout), .Less(1'b0),
    .Ainvert(Ainvert), .Binvert(Binvert), .CarryOut(mips_ula1bit_set_13_carryout), .Resultado(Saida[12]),
    .\Operação (\Operação ));  // open: Set
  mips_ULA1bit_set mips_ula1bit_set_14 (
    .A(Entrada0[13]), .B(Entrada1[13]), .CarryIn(mips_ula1bit_set_13_carryout), .Less(1'b0),
    .Ainvert(Ainvert), .Binvert(Binvert), .CarryOut(mips_ula1bit_set_14_carryout), .Resultado(Saida[13]),
    .\Operação (\Operação ));  // open: Set
  mips_ULA1bit_set mips_ula1bit_set_15 (
    .A(Entrada0[14]), .B(Entrada1[14]), .CarryIn(mips_ula1bit_set_14_carryout), .Less(1'b0),
    .Ainvert(Ainvert), .Binvert(Binvert), .CarryOut(mips_ula1bit_set_15_carryout), .Resultado(Saida[14]),
    .\Operação (\Operação ));  // open: Set
  mips_ULA1bit_set mips_ula1bit_set_16 (
    .A(Entrada0[15]), .B(Entrada1[15]), .CarryIn(mips_ula1bit_set_15_carryout), .Less(1'b0),
    .Ainvert(Ainvert), .Binvert(Binvert), .CarryOut(mips_ula1bit_set_16_carryout), .Resultado(Saida[15]),
    .\Operação (\Operação ));  // open: Set
  mips_ULA1bit_set mips_ula1bit_set_17 (
    .A(Entrada0[16]), .B(Entrada1[16]), .CarryIn(mips_ula1bit_set_16_carryout), .Less(1'b0),
    .Ainvert(Ainvert), .Binvert(Binvert), .CarryOut(mips_ula1bit_set_17_carryout), .Resultado(Saida[16]),
    .\Operação (\Operação ));  // open: Set
  mips_ULA1bit_set mips_ula1bit_set_18 (
    .A(Entrada0[17]), .B(Entrada1[17]), .CarryIn(mips_ula1bit_set_17_carryout), .Less(1'b0),
    .Ainvert(Ainvert), .Binvert(Binvert), .CarryOut(mips_ula1bit_set_18_carryout), .Resultado(Saida[17]),
    .\Operação (\Operação ));  // open: Set
  mips_ULA1bit_set mips_ula1bit_set_19 (
    .A(Entrada0[18]), .B(Entrada1[18]), .CarryIn(mips_ula1bit_set_18_carryout), .Less(1'b0),
    .Ainvert(Ainvert), .Binvert(Binvert), .CarryOut(mips_ula1bit_set_19_carryout), .Resultado(Saida[18]),
    .\Operação (\Operação ));  // open: Set
  mips_ULA1bit_set mips_ula1bit_set_20 (
    .A(Entrada0[19]), .B(Entrada1[19]), .CarryIn(mips_ula1bit_set_19_carryout), .Less(1'b0),
    .Ainvert(Ainvert), .Binvert(Binvert), .CarryOut(mips_ula1bit_set_20_carryout), .Resultado(Saida[19]),
    .\Operação (\Operação ));  // open: Set
  mips_ULA1bit_set mips_ula1bit_set_21 (
    .A(Entrada0[20]), .B(Entrada1[20]), .CarryIn(mips_ula1bit_set_20_carryout), .Less(1'b0),
    .Ainvert(Ainvert), .Binvert(Binvert), .CarryOut(mips_ula1bit_set_21_carryout), .Resultado(Saida[20]),
    .\Operação (\Operação ));  // open: Set
  mips_ULA1bit_set mips_ula1bit_set_22 (
    .A(Entrada0[21]), .B(Entrada1[21]), .CarryIn(mips_ula1bit_set_21_carryout), .Less(1'b0),
    .Ainvert(Ainvert), .Binvert(Binvert), .CarryOut(mips_ula1bit_set_22_carryout), .Resultado(Saida[21]),
    .\Operação (\Operação ));  // open: Set
  mips_ULA1bit_set mips_ula1bit_set_23 (
    .A(Entrada0[22]), .B(Entrada1[22]), .CarryIn(mips_ula1bit_set_22_carryout), .Less(1'b0),
    .Ainvert(Ainvert), .Binvert(Binvert), .CarryOut(mips_ula1bit_set_23_carryout), .Resultado(Saida[22]),
    .\Operação (\Operação ));  // open: Set
  mips_ULA1bit_set mips_ula1bit_set_24 (
    .A(Entrada0[23]), .B(Entrada1[23]), .CarryIn(mips_ula1bit_set_23_carryout), .Less(1'b0),
    .Ainvert(Ainvert), .Binvert(Binvert), .CarryOut(mips_ula1bit_set_24_carryout), .Resultado(Saida[23]),
    .\Operação (\Operação ));  // open: Set
  mips_ULA1bit_set mips_ula1bit_set_25 (
    .A(Entrada0[24]), .B(Entrada1[24]), .CarryIn(mips_ula1bit_set_24_carryout), .Less(1'b0),
    .Ainvert(Ainvert), .Binvert(Binvert), .CarryOut(mips_ula1bit_set_25_carryout), .Resultado(Saida[24]),
    .\Operação (\Operação ));  // open: Set
  mips_ULA1bit_set mips_ula1bit_set_26 (
    .A(Entrada0[25]), .B(Entrada1[25]), .CarryIn(mips_ula1bit_set_25_carryout), .Less(1'b0),
    .Ainvert(Ainvert), .Binvert(Binvert), .CarryOut(mips_ula1bit_set_26_carryout), .Resultado(Saida[25]),
    .\Operação (\Operação ));  // open: Set
  mips_ULA1bit_set mips_ula1bit_set_27 (
    .A(Entrada0[26]), .B(Entrada1[26]), .CarryIn(mips_ula1bit_set_26_carryout), .Less(1'b0),
    .Ainvert(Ainvert), .Binvert(Binvert), .CarryOut(mips_ula1bit_set_27_carryout), .Resultado(Saida[26]),
    .\Operação (\Operação ));  // open: Set
  mips_ULA1bit_set mips_ula1bit_set_28 (
    .A(Entrada0[27]), .B(Entrada1[27]), .CarryIn(mips_ula1bit_set_27_carryout), .Less(1'b0),
    .Ainvert(Ainvert), .Binvert(Binvert), .CarryOut(mips_ula1bit_set_28_carryout), .Resultado(Saida[27]),
    .\Operação (\Operação ));  // open: Set
  mips_ULA1bit_set mips_ula1bit_set_29 (
    .A(Entrada0[28]), .B(Entrada1[28]), .CarryIn(mips_ula1bit_set_28_carryout), .Less(1'b0),
    .Ainvert(Ainvert), .Binvert(Binvert), .CarryOut(mips_ula1bit_set_29_carryout), .Resultado(Saida[28]),
    .\Operação (\Operação ));  // open: Set
  mips_ULA1bit_set mips_ula1bit_set_30 (
    .A(Entrada0[29]), .B(Entrada1[29]), .CarryIn(mips_ula1bit_set_29_carryout), .Less(1'b0),
    .Ainvert(Ainvert), .Binvert(Binvert), .CarryOut(mips_ula1bit_set_30_carryout), .Resultado(Saida[29]),
    .\Operação (\Operação ));  // open: Set
  mips_ULA1bit_set mips_ula1bit_set_31 (
    .A(Entrada0[30]), .B(Entrada1[30]), .CarryIn(mips_ula1bit_set_30_carryout), .Less(1'b0),
    .Ainvert(Ainvert), .Binvert(Binvert), .CarryOut(mips_ula1bit_set_31_carryout), .Resultado(Saida[30]),
    .\Operação (\Operação ));  // open: Set
  mips_ULA1bit_set mips_ula1bit_set_32 (
    .A(Entrada0[31]), .B(Entrada1[31]), .CarryIn(mips_ula1bit_set_31_carryout), .Less(1'b0),
    .Ainvert(Ainvert), .Binvert(Binvert), .CarryOut(CarryOut), .Resultado(Saida[31]),
    .\Operação (\Operação ), .Set(mips_ula1bit_set_32_set));
  // Pins of 1 and 2 bits meet at \Operação 
  // Pins of 1 and 32 bits meet at Saida
endmodule

/* Test case:
	Operação	A	B	Ainvert		Binvert		CarryIn		Result31	Result30	Result29	Result28	Result27	Result26	Result25	Result24	Result23	Result22	Result21	Result20	Result19	Result18	Result17	Result16	Result15	Result14	Result13	Result12	Result11	Result10	Result9		Result8		Result7		Result6		Result5		Result4		Result3		Result2		Result1		Result0
loop(a,32)
	loop(b,32)
		0	(a)	(b)	0	0	0	bits(32,a&b)
		1	(a)	(b)	0	0	0	bits(32,a|b)
		10	(a)	(b)	0	0	0	bits(32,a+b)
		10	(a)	(b)	0	1	1	bits(32,a-b)
		0	(a)	(b)	1	1	0	bits(32,~(a|b))
		11	(a)	(b)	0	1	1	bits(32,a-b>31)
	end loop
end loop
*/
