// Digital circuit mips_ULA8bits.dig as structural Verilog
module mips_ULA8bits (
  input  A0,
  input  B0,
  input  Binvert,
  input  Ainvert,
  input  CarryIn,
  input  [1:0] \Operação ,
  input  A1,
  input  B1,
  input  A2,
  input  B2,
  input  A3,
  input  B3,
  input  A4,
  input  B4,
  input  A5,
  input  B5,
  input  A6,
  input  B6,
  input  A7,
  input  B7,
  output Result0,
  output Result1,
  output Result2,
  output Result3,
  output Result4,
  output Result5,
  output Result6,
  output Result7
);

  wire mips_ula1bit_1_carryout, mips_ula1bit_2_carryout, mips_ula1bit_3_carryout, mips_ula1bit_4_carryout,
       mips_ula1bit_5_carryout, mips_ula1bit_6_carryout, mips_ula1bit_7_carryout, mips_ula1bit_8_carryout;

  mips_ULA1bit mips_ula1bit_1 (
    .A(A0), .B(B0), .CarryIn(CarryIn), .Less(mips_ula1bit_8_carryout), .Ainvert(Ainvert), .Binvert(Binvert),
    .\Operação (\Operação ), .CarryOut(mips_ula1bit_1_carryout), .Resultado(Result0));
  mips_ULA1bit mips_ula1bit_2 (
    .A(A1), .B(B1), .CarryIn(mips_ula1bit_1_carryout), .Less(1'b0), .Ainvert(Ainvert), .Binvert(Binvert),
    .\Operação (\Operação ), .CarryOut(mips_ula1bit_2_carryout), .Resultado(Result1));
  mips_ULA1bit mips_ula1bit_3 (
    .A(A2), .B(B2), .CarryIn(mips_ula1bit_2_carryout), .Less(1'b0), .Ainvert(Ainvert), .Binvert(Binvert),
    .\Operação (\Operação ), .CarryOut(mips_ula1bit_3_carryout), .Resultado(Result2));
  mips_ULA1bit mips_ula1bit_4 (
    .A(A3), .B(B3), .CarryIn(mips_ula1bit_3_carryout), .Less(1'b0), .Ainvert(Ainvert), .Binvert(Binvert),
    .\Operação (\Operação ), .CarryOut(mips_ula1bit_4_carryout), .Resultado(Result3));
  mips_ULA1bit mips_ula1bit_5 (
    .A(A4), .B(B4), .CarryIn(mips_ula1bit_4_carryout), .Less(1'b0), .Ainvert(Ainvert), .Binvert(Binvert),
    .\Operação (\Operação ), .CarryOut(mips_ula1bit_5_carryout), .Resultado(Result4));
  mips_ULA1bit mips_ula1bit_6 (
    .A(A5), .B(B5), .CarryIn(mips_ula1bit_5_carryout), .Less(1'b0), .Ainvert(Ainvert), .Binvert(Binvert),
    .\Operação (\Operação ), .CarryOut(mips_ula1bit_6_carryout), .Resultado(Result5));
  mips_ULA1bit mips_ula1bit_7 (
    .A(A6), .B(B6), .CarryIn(mips_ula1bit_6_carryout), .Less(1'b0), .Ainvert(Ainvert), .Binvert(Binvert),
    .\Operação (\Operação ), .CarryOut(mips_ula1bit_7_carryout), .Resultado(Result6));
  mips_ULA1bit mips_ula1bit_8 (
    .A(A7), .B(B7), .CarryIn(mips_ula1bit_7_carryout), .Less(1'b0), .Ainvert(Ainvert), .Binvert(Binvert),
    .\Operação (\Operação ), .CarryOut(mips_ula1bit_8_carryout), .Resultado(Result7));
  // Pins of 1 and 2 bits meet at \Operação 
endmodule
