// Digital circuit mips_aux.dig as structural Verilog
module mips_aux (
);

  wire mips_memoria_dado_1_p1, mips_memoria_dado_1_p3, mips_memoria_dado_1_p4;
  wire [27:0] \mips_deslocamento26_28_1_saída ;
  wire [31:0] \mips_memoria_instrução_1_d , undriven;

  \mips_memoria_instrução  \mips_memoria_instrução_1  (.A(undriven), .D(\mips_memoria_instrução_1_d ));
  mips_deslocamento26_28 mips_deslocamento26_28_1 (
    .Entrada(\mips_memoria_instrução_1_d [25:0]), .\Saída (\mips_deslocamento26_28_1_saída ));
  // mips_controle mips_controle_1: pin names not known; wires that end beside it: \mips_memoria_instrução_1_d [31:26]
  mips_bancodeReg mips_bancodereg_1 ();
  mips_extensor16_32 mips_extensor16_32_1 (.Entrada(\mips_memoria_instrução_1_d [15:0]));  // open: Saída
  mips_ULA32bits_newmodel mips_ula32bits_newmodel_1 ();  // open: Binvert, Ainvert, CarryIn, Operação, Entrada0, Entrada1, CarryOut, Saida
  // mips_memoria_dado mips_memoria_dado_1: pin names not known; wires that end beside it: mips_memoria_dado_1_p1, mips_memoria_dado_1_p1, mips_memoria_dado_1_p3, mips_memoria_dado_1_p4, mips_memoria_dado_1_p4
endmodule
