// Digital circuit mips_auxiliar.dig as structural Verilog
module mips_auxiliar (
  input  A,
  input  Entrada0,
  input  Entrada1,
  input  Entrada2,
  input  Entrada3,
  input  Entrada4,
  input  Entrada5,
  input  Entrada6,
  input  Entrada7,
  input  Entrada8,
  input  Entrada9,
  input  Entrada10,
  input  Entrada11,
  input  Entrada12,
  input  Entrada13,
  input  Entrada14,
  input  Entrada15,
  output SAIDA0,
  output SAIDA1,
  output SAIDA2,
  output SAIDA3,
  output SAIDA4,
  output SAIDA5,
  output SAIDA6,
  output SAIDA7,
  output SAIDA8,
  output SAIDA9,
  output SAIDA10,
  output SAIDA11,
  output SAIDA12,
  output SAIDA13,
  output SAIDA14,
  output SAIDA15
);

  and and_1 (SAIDA0, A, Entrada0);
  and and_2 (SAIDA1, A, Entrada1);
  and and_3 (SAIDA2, A, Entrada2);
  and and_4 (SAIDA3, A, Entrada3);
  and and_5 (SAIDA4, A, Entrada4);
  and and_6 (SAIDA5, A, Entrada5);
  and and_7 (SAIDA6, A, Entrada6);
  and and_8 (SAIDA7, A, Entrada7);
  and and_9 (SAIDA8, A, Entrada8);
  and and_10 (SAIDA9, A, Entrada9);
  and and_11 (SAIDA10, A, Entrada10);
  and and_12 (SAIDA11, A, Entrada11);
  and and_13 (SAIDA12, A, Entrada12);
  and and_14 (SAIDA13, A, Entrada13);
  and and_15 (SAIDA14, A, Entrada14);
  and and_16 (SAIDA15, A, Entrada15);
endmodule
