// Digital circuit mips_auxiliar_lixo.dig as structural Verilog
module mips_auxiliar_lixo (
);

  mips_decodificador mips_decodificador_1 ();  // open: Entrada, Saida0, Saida1, Saida2, Saida3, Saida4, Saida5, Saida6, Saida7, Saida8, Saida9, Saida10, Saida11, Saida12, Saida13, Saida14, Saida15, Saida16, Saida17, Saida18, Saida19, Saida20, Saida21, Saida22, Saida23, Saida24, Saida25, Saida26, Saida27, Saida28, Saida29, Saida30, Saida31
endmodule
