// Digital circuit mips_bancodeReg.dig as structural Verilog
module mips_bancodeReg (
  input  Sinal_de_Escrita,
  input  [31:0] Dados_do_Registrador,
  input  Numero_do_Registrador,
  input  [4:0] Registrador_de_leitura_1,
  input  [4:0] Registrador_de_Leitura_2,
  output [31:0] Dados_de_Leitura_1,
  output [31:0] Dados_de_Leitura_2
);

  wire and_1_out, and_2_out, and_3_out, and_4_out, and_5_out, and_6_out, and_7_out, and_8_out, and_9_out,
       and_10_out, and_11_out, and_12_out, and_13_out, and_14_out, and_15_out, and_16_out, and_17_out,
       and_18_out, and_19_out, and_20_out, and_21_out, and_22_out, and_23_out, and_24_out, and_25_out,
       and_26_out, and_27_out, and_28_out, and_29_out, and_30_out, and_31_out, and_32_out,
       mips_decodificador_1_saida0, mips_decodificador_1_saida1, mips_decodificador_1_saida2,
       mips_decodificador_1_saida3, mips_decodificador_1_saida4, mips_decodificador_1_saida5,
       mips_decodificador_1_saida6, mips_decodificador_1_saida7, mips_decodificador_1_saida8,
       mips_decodificador_1_saida9, mips_decodificador_1_saida10, mips_decodificador_1_saida11,
       mips_decodificador_1_saida12, mips_decodificador_1_saida13, mips_decodificador_1_saida14,
       mips_decodificador_1_saida15, mips_decodificador_1_saida16, mips_decodificador_1_saida17,
       mips_decodificador_1_saida18, mips_decodificador_1_saida19, mips_decodificador_1_saida20,
       mips_decodificador_1_saida21, mips_decodificador_1_saida22, mips_decodificador_1_saida23,
       mips_decodificador_1_saida24, mips_decodificador_1_saida25, mips_decodificador_1_saida26,
       mips_decodificador_1_saida27, mips_decodificador_1_saida28, mips_decodificador_1_saida29,
       mips_decodificador_1_saida30, mips_decodificador_1_saida31;
  wire [31:0] mips_reg32bits_1_saida, mips_reg32bits_2_saida, mips_reg32bits_3_saida, mips_reg32bits_4_saida,
       mips_reg32bits_5_saida, mips_reg32bits_6_saida, mips_reg32bits_7_saida, mips_reg32bits_8_saida,
       mips_reg32bits_9_saida, mips_reg32bits_10_saida, mips_reg32bits_11_saida, mips_reg32bits_12_saida,
       mips_reg32bits_13_saida, mips_reg32bits_14_saida, mips_reg32bits_15_saida, mips_reg32bits_16_saida,
       mips_reg32bits_17_saida, mips_reg32bits_18_saida, mips_reg32bits_19_saida, mips_reg32bits_20_saida,
       mips_reg32bits_21_saida, mips_reg32bits_22_saida, mips_reg32bits_23_saida, mips_reg32bits_24_saida,
       mips_reg32bits_25_saida, mips_reg32bits_26_saida, mips_reg32bits_27_saida, mips_reg32bits_28_saida,
       mips_reg32bits_29_saida, mips_reg32bits_30_saida, mips_reg32bits_31_saida, mips_reg32bits_32_saida;

  mips_decodificador mips_decodificador_1 (
    .C(Numero_do_Registrador), .Saida0(mips_decodificador_1_saida0), .Saida1(mips_decodificador_1_saida1),
    .Saida2(mips_decodificador_1_saida2), .Saida3(mips_decodificador_1_saida3),
    .Saida4(mips_decodificador_1_saida4), .Saida5(mips_decodificador_1_saida5),
    .Saida6(mips_decodificador_1_saida6), .Saida7(mips_decodificador_1_saida7),
    .Saida8(mips_decodificador_1_saida8), .Saida9(mips_decodificador_1_saida9),
    .Saida10(mips_decodificador_1_saida10), .Saida11(mips_decodificador_1_saida11),
    .Saida12(mips_decodificador_1_saida12), .Saida13(mips_decodificador_1_saida13),
    .Saida14(mips_decodificador_1_saida14), .Saida15(mips_decodificador_1_saida15),
    .Saida16(mips_decodificador_1_saida16), .Saida17(mips_decodificador_1_saida17),
    .Saida18(mips_decodificador_1_saida18), .Saida19(mips_decodificador_1_saida19),
    .Saida20(mips_decodificador_1_saida20), .Saida21(mips_decodificador_1_saida21),
    .Saida22(mips_decodificador_1_saida22), .Saida23(mips_decodificador_1_saida23),
    .Saida24(mips_decodificador_1_saida24), .Saida25(mips_decodificador_1_saida25),
    .Saida26(mips_decodificador_1_saida26), .Saida27(mips_decodificador_1_saida27),
    .Saida28(mips_decodificador_1_saida28), .Saida29(mips_decodificador_1_saida29),
    .Saida30(mips_decodificador_1_saida30), .Saida31(mips_decodificador_1_saida31));  // open: D, B, A, E
  and and_1 (and_1_out, Sinal_de_Escrita, mips_decodificador_1_saida0);
  and and_2 (and_2_out, Sinal_de_Escrita, mips_decodificador_1_saida1);
  and and_3 (and_3_out, Sinal_de_Escrita, mips_decodificador_1_saida2);
  and and_4 (and_4_out, Sinal_de_Escrita, mips_decodificador_1_saida3);
  and and_5 (and_5_out, Sinal_de_Escrita, mips_decodificador_1_saida4);
  and and_6 (and_6_out, Sinal_de_Escrita, mips_decodificador_1_saida5);
  and and_7 (and_7_out, Sinal_de_Escrita, mips_decodificador_1_saida6);
  and and_8 (and_8_out, Sinal_de_Escrita, mips_decodificador_1_saida7);
  and and_9 (and_9_out, Sinal_de_Escrita, mips_decodificador_1_saida8);
  and and_10 (and_10_out, Sinal_de_Escrita, mips_decodificador_1_saida9);
  and and_11 (and_11_out, Sinal_de_Escrita, mips_decodificador_1_saida10);
  and and_12 (and_12_out, Sinal_de_Escrita, mips_decodificador_1_saida11);
  and and_13 (and_13_out, Sinal_de_Escrita, mips_decodificador_1_saida12);
  and and_14 (and_14_out, Sinal_de_Escrita, mips_decodificador_1_saida13);
  and and_15 (and_15_out, Sinal_de_Escrita, mips_decodificador_1_saida14);
  and and_16 (and_16_out, Sinal_de_Escrita, mips_decodificador_1_saida15);
  and and_17 (and_17_out, Sinal_de_Escrita, mips_decodificador_1_saida16);
  and and_18 (and_18_out, Sinal_de_Escrita, mips_decodificador_1_saida17);
  and and_19 (and_19_out, Sinal_de_Escrita, mips_decodificador_1_saida18);
  and and_20 (and_20_out, Sinal_de_Escrita, mips_decodificador_1_saida19);
  and and_21 (and_21_out, Sinal_de_Escrita, mips_decodificador_1_saida20);
  and and_22 (and_22_out, Sinal_de_Escrita, mips_decodificador_1_saida21);
  and and_23 (and_23_out, Sinal_de_Escrita, mips_decodificador_1_saida22);
  and and_24 (and_24_out, Sinal_de_Escrita, mips_decodificador_1_saida23);
  and and_25 (and_25_out, Sinal_de_Escrita, mips_decodificador_1_saida24);
  and and_26 (and_26_out, Sinal_de_Escrita, mips_decodificador_1_saida25);
  and and_27 (and_27_out, Sinal_de_Escrita, mips_decodificador_1_saida26);
  and and_28 (and_28_out, Sinal_de_Escrita, mips_decodificador_1_saida27);
  and and_29 (and_29_out, Sinal_de_Escrita, mips_decodificador_1_saida28);
  and and_30 (and_30_out, Sinal_de_Escrita, mips_decodificador_1_saida29);
  and and_31 (and_31_out, Sinal_de_Escrita, mips_decodificador_1_saida30);
  and and_32 (and_32_out, Sinal_de_Escrita, mips_decodificador_1_saida31);
  mips_reg32bits mips_reg32bits_1 (.Entrada(Dados_do_Registrador), .Clock(and_1_out), .Saida(mips_reg32bits_1_saida));
  mips_reg32bits mips_reg32bits_2 (.Entrada(Dados_do_Registrador), .Clock(and_2_out), .Saida(mips_reg32bits_2_saida));
  mips_reg32bits mips_reg32bits_3 (.Entrada(Dados_do_Registrador), .Clock(and_3_out), .Saida(mips_reg32bits_3_saida));
  mips_reg32bits mips_reg32bits_4 (.Entrada(Dados_do_Registrador), .Clock(and_4_out), .Saida(mips_reg32bits_4_saida));
  mips_reg32bits mips_reg32bits_5 (.Entrada(Dados_do_Registrador), .Clock(and_5_out), .Saida(mips_reg32bits_5_saida));
  mips_reg32bits mips_reg32bits_6 (.Entrada(Dados_do_Registrador), .Clock(and_6_out), .Saida(mips_reg32bits_6_saida));
  mips_reg32bits mips_reg32bits_7 (.Entrada(Dados_do_Registrador), .Clock(and_7_out), .Saida(mips_reg32bits_7_saida));
  mips_reg32bits mips_reg32bits_8 (.Entrada(Dados_do_Registrador), .Clock(and_8_out), .Saida(mips_reg32bits_8_saida));
  mips_reg32bits mips_reg32bits_9 (.Entrada(Dados_do_Registrador), .Clock(and_9_out), .Saida(mips_reg32bits_9_saida));
  mips_reg32bits mips_reg32bits_10 (
    .Entrada(Dados_do_Registrador), .Clock(and_10_out), .Saida(mips_reg32bits_10_saida));
  mips_reg32bits mips_reg32bits_11 (
    .Entrada(Dados_do_Registrador), .Clock(and_11_out), .Saida(mips_reg32bits_11_saida));
  mips_reg32bits mips_reg32bits_12 (
    .Entrada(Dados_do_Registrador), .Clock(and_12_out), .Saida(mips_reg32bits_12_saida));
  mips_reg32bits mips_reg32bits_13 (
    .Entrada(Dados_do_Registrador), .Clock(and_13_out), .Saida(mips_reg32bits_13_saida));
  mips_reg32bits mips_reg32bits_14 (
    .Entrada(Dados_do_Registrador), .Clock(and_14_out), .Saida(mips_reg32bits_14_saida));
  mips_reg32bits mips_reg32bits_15 (
    .Entrada(Dados_do_Registrador), .Clock(and_15_out), .Saida(mips_reg32bits_15_saida));
  mips_reg32bits mips_reg32bits_16 (
    .Entrada(Dados_do_Registrador), .Clock(and_16_out), .Saida(mips_reg32bits_16_saida));
  mips_reg32bits mips_reg32bits_17 (
    .Entrada(Dados_do_Registrador), .Clock(and_17_out), .Saida(mips_reg32bits_17_saida));
  mips_reg32bits mips_reg32bits_18 (
    .Entrada(Dados_do_Registrador), .Clock(and_18_out), .Saida(mips_reg32bits_18_saida));
  mips_reg32bits mips_reg32bits_19 (
    .Entrada(Dados_do_Registrador), .Clock(and_19_out), .Saida(mips_reg32bits_19_saida));
  mips_reg32bits mips_reg32bits_20 (
    .Entrada(Dados_do_Registrador), .Clock(and_20_out), .Saida(mips_reg32bits_20_saida));
  mips_reg32bits mips_reg32bits_21 (
    .Entrada(Dados_do_Registrador), .Clock(and_21_out), .Saida(mips_reg32bits_21_saida));
  mips_reg32bits mips_reg32bits_22 (
    .Entrada(Dados_do_Registrador), .Clock(and_22_out), .Saida(mips_reg32bits_22_saida));
  mips_reg32bits mips_reg32bits_23 (
    .Entrada(Dados_do_Registrador), .Clock(and_23_out), .Saida(mips_reg32bits_23_saida));
  mips_reg32bits mips_reg32bits_24 (
    .Entrada(Dados_do_Registrador), .Clock(and_24_out), .Saida(mips_reg32bits_24_saida));
  mips_reg32bits mips_reg32bits_25 (
    .Entrada(Dados_do_Registrador), .Clock(and_25_out), .Saida(mips_reg32bits_25_saida));
  mips_reg32bits mips_reg32bits_26 (
    .Entrada(Dados_do_Registrador), .Clock(and_26_out), .Saida(mips_reg32bits_26_saida));
  mips_reg32bits mips_reg32bits_27 (
    .Entrada(Dados_do_Registrador), .Clock(and_27_out), .Saida(mips_reg32bits_27_saida));
  mips_reg32bits mips_reg32bits_28 (
    .Entrada(Dados_do_Registrador), .Clock(and_28_out), .Saida(mips_reg32bits_28_saida));
  mips_reg32bits mips_reg32bits_29 (
    .Entrada(Dados_do_Registrador), .Clock(and_29_out), .Saida(mips_reg32bits_29_saida));
  mips_reg32bits mips_reg32bits_30 (
    .Entrada(Dados_do_Registrador), .Clock(and_30_out), .Saida(mips_reg32bits_30_saida));
  mips_reg32bits mips_reg32bits_31 (
    .Entrada(Dados_do_Registrador), .Clock(and_31_out), .Saida(mips_reg32bits_31_saida));
  mips_reg32bits mips_reg32bits_32 (
    .Entrada(Dados_do_Registrador), .Clock(and_32_out), .Saida(mips_reg32bits_32_saida));
  mips_mux32 mips_mux32_1 (
    .Entrada0(mips_reg32bits_1_saida), .Entrada1(mips_reg32bits_2_saida), .Entrada2(mips_reg32bits_3_saida),
    .Entrada3(mips_reg32bits_4_saida), .Entrada4(mips_reg32bits_5_saida), .Entrada5(mips_reg32bits_6_saida),
    .Entrada6(mips_reg32bits_7_saida), .Entrada7(mips_reg32bits_8_saida), .Entrada8(mips_reg32bits_9_saida),
    .Entrada9(mips_reg32bits_10_saida), .Entrada10(mips_reg32bits_11_saida),
    .Entrada11(mips_reg32bits_12_saida), .Entrada12(mips_reg32bits_13_saida),
    .Entrada13(mips_reg32bits_14_saida), .Entrada14(mips_reg32bits_15_saida),
    .Entrada15(mips_reg32bits_16_saida), .Entrada16(mips_reg32bits_17_saida),
    .Entrada17(mips_reg32bits_18_saida), .Entrada18(mips_reg32bits_19_saida),
    .Entrada19(mips_reg32bits_20_saida), .Entrada20(mips_reg32bits_21_saida),
    .Entrada21(mips_reg32bits_22_saida), .Entrada22(mips_reg32bits_23_saida),
    .Entrada23(mips_reg32bits_24_saida), .Entrada24(mips_reg32bits_25_saida),
    .Entrada25(mips_reg32bits_26_saida), .Entrada26(mips_reg32bits_27_saida),
    .Entrada27(mips_reg32bits_28_saida), .Entrada28(mips_reg32bits_29_saida),
    .Entrada29(mips_reg32bits_30_saida), .Entrada30(mips_reg32bits_31_saida),
    .Entrada31(mips_reg32bits_32_saida), .\Seleção (Registrador_de_leitura_1), .Saida(Dados_de_Leitura_1));
  mips_mux32 mips_mux32_2 (
    .Entrada0(mips_reg32bits_1_saida), .Entrada1(mips_reg32bits_2_saida), .Entrada2(mips_reg32bits_3_saida),
    .Entrada3(mips_reg32bits_4_saida), .Entrada4(mips_reg32bits_5_saida), .Entrada5(mips_reg32bits_6_saida),
    .Entrada6(mips_reg32bits_7_saida), .Entrada7(mips_reg32bits_8_saida), .Entrada8(mips_reg32bits_9_saida),
    .Entrada9(mips_reg32bits_10_saida), .Entrada10(mips_reg32bits_11_saida),
    .Entrada11(mips_reg32bits_12_saida), .Entrada12(mips_reg32bits_13_saida),
    .Entrada13(mips_reg32bits_14_saida), .Entrada14(mips_reg32bits_15_saida),
    .Entrada15(mips_reg32bits_16_saida), .Entrada16(mips_reg32bits_17_saida),
    .Entrada17(mips_reg32bits_18_saida), .Entrada18(mips_reg32bits_19_saida),
    .Entrada19(mips_reg32bits_20_saida), .Entrada20(mips_reg32bits_21_saida),
    .Entrada21(mips_reg32bits_22_saida), .Entrada23(mips_reg32bits_24_saida),
    .Entrada26(mips_reg32bits_27_saida), .Entrada27(mips_reg32bits_28_saida),
    .Entrada28(mips_reg32bits_29_saida), .Entrada29(mips_reg32bits_30_saida),
    .Entrada30(mips_reg32bits_31_saida), .Entrada31(mips_reg32bits_32_saida),
    .\Seleção (Registrador_de_Leitura_2), .Saida(Dados_de_Leitura_2));  // open: Entrada22, Entrada24, Entrada25
  // Pins of 1 and 32 bits meet at Dados_de_Leitura_2
endmodule
