// Digital circuit mips_controle.dig as structural Verilog
module mips_controle (
  input  [5:0] Op,
  output RegDst,
  output ALUScr,
  output MemParaReg,
  output EscreveReg,
  output LeMem,
  output EscreveMem,
  output Branch,
  output ALUOp0,
  output ALUOp1,
  output jump
);

  wire and_2_out, and_3_out, not_1_out, not_2_out, not_3_out, not_4_out, not_5_out, not_6_out;

  not not_1 (not_1_out, Op[0]);
  not not_2 (not_2_out, Op[1]);
  not not_3 (not_3_out, Op[2]);
  not not_4 (not_4_out, Op[3]);
  not not_5 (not_5_out, Op[4]);
  not not_6 (not_6_out, Op[5]);
  and and_1 (RegDst, not_3_out, not_6_out);
  or or_1 (ALUScr, Op[2], Op[5]);
  and and_2 (and_2_out, Op[0], not_2_out, not_3_out, not_4_out, Op[4], Op[5]);
  and and_3 (and_3_out, not_1_out, not_2_out, not_4_out, not_5_out, not_6_out);
  and and_4 (LeMem, Op[0], not_2_out, not_3_out, not_4_out, Op[4], Op[5]);
  and and_5 (EscreveMem, Op[0], not_2_out, Op[2], not_4_out, Op[4], Op[5]);
  and and_6 (ALUOp0, not_3_out, not_4_out, not_6_out);
  and and_7 (jump, not_1_out, not_2_out, not_3_out, not_4_out, Op[4], not_6_out);
  or or_2 (EscreveReg, and_2_out, and_3_out);

  assign ALUOp1 = Op[3];
  assign Branch = Op[3];
  assign MemParaReg = Op[5];

  // Notes on the sheet:
  //   10XX0X
  //   01101X
  //   00010X
  //   000001
  //   01XX0X
  //   001000
  //   10000X
  //   110010
endmodule
