// Digital circuit mips_decodificador2entradas.dig as structural Verilog
module mips_decodificador2entradas (
  input  A,
  input  B,
  input  C,
  input  D,
  input  E,
  output Saida0,
  output Saida1,
  output Saida2,
  output Saida3,
  output Saida4,
  output Saida5,
  output Saida6,
  output Saida7,
  output Saida8,
  output Saida9,
  output Saida10,
  output Saida11,
  output Saida12,
  output Saida13,
  output Saida14,
  output Saida15
);

  wire and_1_out, and_2_out, and_3_out, and_4_out, and_5_out, and_6_out, and_7_out, and_8_out, and_9_out,
       and_10_out, and_11_out, and_12_out, and_13_out, and_14_out, and_15_out, and_16_out, not_1_out,
       not_2_out, not_3_out, not_4_out;

  not not_1 (not_1_out, B);
  not not_2 (not_2_out, C);
  not not_3 (not_3_out, D);
  not not_4 (not_4_out, E);
  and and_1 (and_1_out, not_1_out, not_2_out, not_3_out, not_4_out);
  and and_2 (and_2_out, not_1_out, not_2_out, not_3_out, E);
  and and_3 (and_3_out, not_1_out, not_2_out, D, not_4_out);
  and and_4 (and_4_out, not_1_out, not_2_out, D, E);
  and and_5 (and_5_out, not_1_out, C, not_3_out, not_4_out);
  and and_6 (and_6_out, not_1_out, C, not_3_out, E);
  and and_7 (and_7_out, not_1_out, C, D, not_4_out);
  and and_8 (and_8_out, not_1_out, C, D, E);
  and and_9 (and_9_out, B, not_2_out, not_3_out, not_4_out);
  and and_10 (and_10_out, B, not_2_out, not_3_out, E);
  and and_11 (and_11_out, B, not_2_out, D, not_4_out);
  and and_12 (and_12_out, B, not_2_out, D, E);
  and and_13 (and_13_out, B, C, not_3_out, not_4_out);
  and and_14 (and_14_out, B, C, not_3_out, E);
  and and_15 (and_15_out, B, C, D, not_4_out);
  and and_16 (and_16_out, B, C, D, E);
  and and_17 (Saida0, and_1_out, A);
  and and_18 (Saida1, and_2_out, A);
  and and_19 (Saida2, and_3_out, A);
  and and_20 (Saida3, and_4_out, A);
  and and_21 (Saida4, and_5_out, A);
  and and_22 (Saida5, and_6_out, A);
  and and_23 (Saida6, and_7_out, A);
  and and_24 (Saida7, and_8_out, A);
  and and_25 (Saida8, and_9_out, A);
  and and_26 (Saida9, and_10_out, A);
  and and_27 (Saida10, and_11_out, A);
  and and_28 (Saida11, and_12_out, A);
  and and_29 (Saida12, and_13_out, A);
  and and_30 (Saida13, and_14_out, A);
  and and_31 (Saida14, and_15_out, A);
  and and_32 (Saida15, and_16_out, A);
endmodule
