// Digital circuit mips_decodificador2entradas_errado.dig as structural Verilog
module mips_decodificador2entradas_errado (
  input  Entrada0,
  input  Entrada1,
  input  Entrada2,
  input  Entrada3,
  input  Entrada4,
  output Saida0,
  output Saida1,
  output Saida2,
  output Saida3,
  output Saida4,
  output Saida5,
  output Saida6,
  output Saida7,
  output Saida8,
  output Saida9,
  output Saida10,
  output Saida11,
  output Saida12,
  output Saida13,
  output Saida14,
  output Saida15,
  output Saida16,
  output Saida17,
  output Saida18,
  output Saida19,
  output Saida20,
  output Saida21,
  output Saida22,
  output Saida23,
  output Saida24,
  output Saida25,
  output Saida26,
  output Saida27,
  output Saida28,
  output Saida29,
  output Saida30,
  output Saida31
);

  // And and_1 has open pins: In_1=open, In_2=open, In_3=open, In_4=open, In_5=open, out=Saida0
  // And and_2 has open pins: In_1=open, In_2=open, In_3=open, In_4=open, In_5=open, out=Saida1
  // And and_3 has open pins: In_1=open, In_2=open, In_3=open, In_4=open, In_5=open, out=Saida2
  // And and_4 has open pins: In_1=open, In_2=open, In_3=open, In_4=open, In_5=open, out=Saida3
  // And and_5 has open pins: In_1=open, In_2=open, In_3=open, In_4=open, In_5=open, out=Saida4
  // And and_6 has open pins: In_1=open, In_2=open, In_3=open, In_4=open, In_5=open, out=Saida5
  // And and_7 has open pins: In_1=open, In_2=open, In_3=open, In_4=open, In_5=open, out=Saida6
  // And and_8 has open pins: In_1=open, In_2=open, In_3=open, In_4=open, In_5=open, out=Saida7
  // And and_9 has open pins: In_1=open, In_2=open, In_3=open, In_4=open, In_5=open, out=Saida8
  // And and_10 has open pins: In_1=open, In_2=open, In_3=open, In_4=open, In_5=open, out=Saida9
  // And and_11 has open pins: In_1=open, In_2=open, In_3=open, In_4=open, In_5=open, out=Saida10
  // And and_12 has open pins: In_1=open, In_2=open, In_3=open, In_4=open, In_5=open, out=Saida11
  // And and_13 has open pins: In_1=open, In_2=open, In_3=open, In_4=open, In_5=open, out=Saida12
  // And and_14 has open pins: In_1=open, In_2=open, In_3=open, In_4=open, In_5=open, out=Saida13
  // And and_15 has open pins: In_1=open, In_2=open, In_3=open, In_4=open, In_5=open, out=Saida14
  // And and_16 has open pins: In_1=open, In_2=open, In_3=open, In_4=open, In_5=open, out=Saida15
  // And and_17 has open pins: In_1=open, In_2=open, In_3=open, In_4=open, In_5=open, out=Saida16
  // And and_18 has open pins: In_1=open, In_2=open, In_3=open, In_4=open, In_5=open, out=Saida17
  // And and_19 has open pins: In_1=open, In_2=open, In_3=open, In_4=open, In_5=open, out=Saida18
  // And and_20 has open pins: In_1=open, In_2=open, In_3=open, In_4=open, In_5=open, out=Saida19
  // And and_21 has open pins: In_1=open, In_2=open, In_3=open, In_4=open, In_5=open, out=Saida20
  // And and_22 has open pins: In_1=open, In_2=open, In_3=open, In_4=open, In_5=open, out=Saida21
  // And and_23 has open pins: In_1=open, In_2=open, In_3=open, In_4=open, In_5=open, out=Saida22
  // And and_24 has open pins: In_1=open, In_2=open, In_3=open, In_4=open, In_5=open, out=Saida23
  // And and_25 has open pins: In_1=open, In_2=open, In_3=open, In_4=open, In_5=open, out=Saida24
  // And and_26 has open pins: In_1=open, In_2=open, In_3=open, In_4=open, In_5=open, out=Saida25
  // And and_27 has open pins: In_1=open, In_2=open, In_3=open, In_4=open, In_5=open, out=Saida26
  // And and_28 has open pins: In_1=open, In_2=open, In_3=open, In_4=open, In_5=open, out=Saida27
  // And and_29 has open pins: In_1=open, In_2=open, In_3=open, In_4=open, In_5=open, out=Saida28
  // And and_30 has open pins: In_1=open, In_2=open, In_3=open, In_4=open, In_5=open, out=Saida29
  // And and_31 has open pins: In_1=open, In_2=open, In_3=open, In_4=open, In_5=open, out=Saida30
  // And and_32 has open pins: In_1=open, In_2=open, In_3=open, In_4=open, In_5=open, out=Saida31
endmodule
