// Digital circuit mips_deslocamento26>28.dig as structural Verilog
module mips_deslocamento26_28 (
  input  [25:0] Entrada,
  output [27:0] \Saída 
);


  assign \Saída  = {Entrada, 2'b00};
endmodule
