// Digital circuit mips_extensor16>32.dig as structural Verilog
module mips_extensor16_32 (
  input  [15:0] Entrada,
  output [31:0] \Saída 
);

  // Pins of 15 and 16 bits meet at Entrada

  assign \Saída [30:0] = {{16{\Saída [31]}}, Entrada[14:0]};
endmodule
