// Digital circuit mips_extensor_errado.dig as structural Verilog
module mips_extensor_errado (
  input  [15:0] Entrada,
  output [31:0] \Saída 
);


  assign \Saída  = {Entrada, {16{1'b0}}};
endmodule
