// Digital circuit mips_flipflopD.dig as structural Verilog
module mips_flipflopD (
  input  Clock,
  input  D,
  output Q,
  output nQ
);

  wire mips_latchd_1_q, not_1_out;

  mips_latchD mips_latchd_1 (.Clock(Clock), .D(D), .Q(mips_latchd_1_q));  // open: nQ
  not not_1 (not_1_out, Clock);
  mips_latchD mips_latchd_2 (.Clock(not_1_out), .D(mips_latchd_1_q), .Q(Q), .nQ(nQ));
endmodule
