// Digital circuit mips_instrução_memoria.dig as structural Verilog
module \mips_instrução_memoria  (
  input  [31:0] A,
  output [31:0] D
);

  ROM #(.AddrBits(24), .isProgramMemory("true"), .Bits(16), .Addr_Bits(15)) rom_1 (
    .A(A[23:0]), .sel(A[31]), .D(D[15:0]));
  // Pins of 24 and 31 bits meet at A[30:0]
  // Pins of 16 and 32 bits meet at D

  // Notes on the sheet:
  //   D: bidirectional data bus
  //   {{de Der bidirektionelle Datenbus}}
  //   A: address bus
  //   {{de Der Adressbus}}
  //   contents of rom_1 (hex, n*v repeats v):
  //   1e,14,2020,1,c,c0,2400,0,4,c,0,8,656c,2057,6c64
endmodule
