// Digital circuit mips_latchD_enable.dig as structural Verilog
module mips_latchD_enable (
  input  Clock,
  input  D,
  input  Enable,
  output Q,
  output nQ
);

  wire and_1_out, and_2_out, nor_1_out, nor_2_out;

  and and_1 (and_1_out, Clock, ~D);  // And
  and and_2 (and_2_out, Clock, D);
  nor nor_1 (nor_1_out, and_1_out, nor_2_out);
  nor nor_2 (nor_2_out, nor_1_out, and_2_out);
  and and_3 (Q, Enable, nor_1_out);
  and and_4 (nQ, nor_2_out, Enable);
endmodule
