// Digital circuit mips_memoria_instrução.dig as structural Verilog
module \mips_memoria_instrução  (
  input  [31:0] A,
  output [31:0] D
);

  ROM #(.AddrBits(24), .Bits(32), .Addr_Bits(15)) rom_1 (.A(A[25:2]), .sel(1'b1), .D(D));

  // Notes on the sheet:
  //   D: bidirectional data bus
  //   {{de Der bidirektionelle Datenbus}}
  //   A: address bus
  //   {{de Der Adressbus}}
  //   contents of rom_1 (hex, n*v repeats v):
  //   1e,14,2020,1,c,c0,2400,0,4,c,0,8,656c,2057,6c64
endmodule
