// Digital circuit mips_mux16.dig as structural Verilog
module mips_mux16 (
  input  Entrada0,
  input  Entrada1,
  input  Entrada2,
  input  Entrada3,
  input  Entrada4,
  input  Entrada5,
  input  Entrada6,
  input  Entrada7,
  input  Entrada8,
  input  Entrada9,
  input  Entrada10,
  input  Entrada11,
  input  Entrada12,
  input  Entrada13,
  input  Entrada14,
  input  Entrada15,
  input  S0,
  input  S1,
  input  S2,
  input  S3,
  output Saida
);

  wire mips_mux4_new_1_saida, mips_mux4_new_2_saida, mips_mux4_new_3_saida, mips_mux4_new_4_saida;

  mips_mux4_new mips_mux4_new_1 (
    .Entrada0(Entrada0), .Entrada1(Entrada1), .Entrada2(Entrada2), .Entrada3(Entrada3), .\Seleção0 (S0),
    .\Seleçao1 (S1), .Saida(mips_mux4_new_1_saida));
  mips_mux4_new mips_mux4_new_2 (
    .Entrada0(Entrada4), .Entrada1(Entrada5), .Entrada2(Entrada6), .Entrada3(Entrada7), .\Seleção0 (S0),
    .\Seleçao1 (S1), .Saida(mips_mux4_new_2_saida));
  mips_mux4_new mips_mux4_new_3 (
    .Entrada0(Entrada8), .Entrada1(Entrada9), .Entrada2(Entrada10), .Entrada3(Entrada11), .\Seleção0 (S0),
    .\Seleçao1 (S1), .Saida(mips_mux4_new_3_saida));
  mips_mux4_new mips_mux4_new_4 (
    .Entrada0(Entrada12), .Entrada1(Entrada13), .Entrada2(Entrada14), .Entrada3(Entrada15), .\Seleção0 (S0),
    .\Seleçao1 (S1), .Saida(mips_mux4_new_4_saida));
  mips_mux4_new mips_mux4_new_5 (
    .Entrada0(mips_mux4_new_1_saida), .Entrada1(mips_mux4_new_2_saida), .Entrada2(mips_mux4_new_3_saida),
    .Entrada3(mips_mux4_new_4_saida), .\Seleção0 (S2), .\Seleçao1 (S3), .Saida(Saida));
endmodule
