// Digital circuit mips_mux16_32bits.dig as structural Verilog
module mips_mux16_32bits (
  input  [31:0] Entrada0,
  input  [31:0] Entrada1,
  input  [31:0] Entrada2,
  input  [31:0] Entrada3,
  input  [31:0] Entrada4,
  input  [31:0] Entrada5,
  input  [31:0] Entrada6,
  input  [31:0] Entrada7,
  input  [31:0] Entrada8,
  input  [31:0] Entrada9,
  input  [31:0] Entrada10,
  input  [31:0] Entrada11,
  input  [31:0] Entrada12,
  input  [31:0] Entrada13,
  input  [31:0] Entrada14,
  input  [31:0] Entrada15,
  input  S0,
  input  S1,
  input  S2,
  input  S3,
  output [31:0] Saida
);

  wire mips_mux4_new_1_p7, mips_mux4_new_2_p7, mips_mux4_new_3_p7, mips_mux4_new_4_p7;

  // mips_mux4_new mips_mux4_new_1: pin names not known; wires that end beside it: Entrada0, Entrada1, Entrada2, Entrada3, S0, S1, mips_mux4_new_1_p7
  // mips_mux4_new mips_mux4_new_2: pin names not known; wires that end beside it: Entrada4, Entrada5, Entrada6, Entrada7, S0, S1, mips_mux4_new_2_p7
  // mips_mux4_new mips_mux4_new_3: pin names not known; wires that end beside it: Entrada8, Entrada9, Entrada10, Entrada11, S0, S1, mips_mux4_new_3_p7
  // mips_mux4_new mips_mux4_new_4: pin names not known; wires that end beside it: Entrada12, Entrada13, Entrada14, Entrada15, S0, S1, mips_mux4_new_4_p7
  mips_mux4_new mips_mux4_new_5 (
    .Entrada0(mips_mux4_new_1_p7), .Entrada1(mips_mux4_new_2_p7), .Entrada2(mips_mux4_new_3_p7),
    .Entrada3(mips_mux4_new_4_p7), .\Seleção0 (S2), .\Seleçao1 (S3));  // open: Saida
endmodule
