// Digital circuit mips_mux2.dig as structural Verilog
module mips_mux2 (
  input  Entrada0,
  input  Entrada1,
  input  \Seleção ,
  output Saida
);

  wire and_1_out, and_2_out, not_1_out;

  not not_1 (not_1_out, \Seleção );
  and and_1 (and_1_out, Entrada0, not_1_out);
  and and_2 (and_2_out, \Seleção , Entrada1);
  or or_1 (Saida, and_1_out, and_2_out);
endmodule
