// Digital circuit mips_mux2_32bits.dig as structural Verilog
module mips_mux2_32bits (
  input  [31:0] Entrada0,
  input  [31:0] Entrada1,
  input  \Seleção ,
  output [31:0] Saida
);

  wire and_1_out, and_2_out;

  and and_1 (and_1_out, Entrada0[0], ~\Seleção );  // And
  and and_2 (and_2_out, \Seleção , Entrada1[0]);
  or or_1 (Saida[0], and_1_out, and_2_out);
  // Pins of 1 and 32 bits meet at Entrada0
  // Pins of 1 and 32 bits meet at Entrada1
  // Pins of 1 and 32 bits meet at Saida
endmodule
