// Digital circuit mips_mux32.dig as structural Verilog
module mips_mux32 (
  input  [31:0] Entrada0,
  input  [31:0] Entrada1,
  input  [31:0] Entrada2,
  input  [31:0] Entrada3,
  input  [31:0] Entrada4,
  input  [31:0] Entrada5,
  input  [31:0] Entrada6,
  input  [31:0] Entrada7,
  input  [31:0] Entrada8,
  input  [31:0] Entrada9,
  input  [31:0] Entrada10,
  input  [31:0] Entrada11,
  input  [31:0] Entrada12,
  input  [31:0] Entrada13,
  input  [31:0] Entrada14,
  input  [31:0] Entrada15,
  input  [31:0] Entrada16,
  input  [31:0] Entrada17,
  input  [31:0] Entrada18,
  input  [31:0] Entrada19,
  input  [31:0] Entrada20,
  input  [31:0] Entrada21,
  input  [31:0] Entrada22,
  input  [31:0] Entrada23,
  input  [31:0] Entrada24,
  input  [31:0] Entrada25,
  input  [31:0] Entrada26,
  input  [31:0] Entrada27,
  input  [31:0] Entrada28,
  input  [31:0] Entrada29,
  input  [31:0] Entrada30,
  input  [31:0] Entrada31,
  input  [4:0] \Seleção ,
  output [31:0] Saida
);

  wire mips_mux16_1_p21, mips_mux16_2_p21, mips_mux16_2_p23;

  // mips_mux16 mips_mux16_1: pin names not known; wires that end beside it: Entrada0, Entrada1, Entrada2, Entrada3, Entrada4, Entrada5, Entrada6, Entrada7, Entrada8, Entrada9, Entrada10, Entrada11, Entrada12, Entrada13, Entrada14, Entrada15, \Seleção [0], \Seleção [1], \Seleção [2], \Seleção [3], mips_mux16_1_p21
  // mips_mux16 mips_mux16_2: pin names not known; wires that end beside it: Entrada16, Entrada17, Entrada18, Entrada19, Entrada20, Entrada21, Entrada22, Entrada23, Entrada24, Entrada25, Entrada26, Entrada27, Entrada28, Entrada29, Entrada30, Entrada31, \Seleção [0], \Seleção [1], \Seleção [2], \Seleção [3], mips_mux16_2_p21, mips_mux16_2_p21, mips_mux16_2_p23
  mips_mux2 mips_mux2_1 (.A(mips_mux16_1_p21), .B(mips_mux16_2_p23), .S(\Seleção [4]));  // open: S_2
endmodule
