// Digital circuit mips_mux4.dig as structural Verilog
module mips_mux4 (
  input  A,
  input  B,
  input  C,
  input  D,
  input  S0,
  input  S1,
  output Saida
);

  wire and_1_out, and_2_out, and_3_out, and_4_out, and_5_out, and_6_out, and_7_out, and_8_out;

  and and_1 (and_1_out, ~S0, ~S1);  // And
  and and_2 (and_2_out, ~S0, S1);  // And
  and and_3 (and_3_out, S0, ~S1);  // And
  and and_4 (and_4_out, S0, S1);
  and and_5 (and_5_out, and_1_out, A);
  and and_6 (and_6_out, and_2_out, B);
  and and_7 (and_7_out, and_3_out, C);
  and and_8 (and_8_out, and_4_out, D);
  or or_1 (Saida, and_5_out, and_6_out, and_7_out, and_8_out);
endmodule
