// Digital circuit mips_mux4_new.dig as structural Verilog
module mips_mux4_new (
  input  Entrada0,
  input  Entrada1,
  input  Entrada2,
  input  Entrada3,
  input  \Seleção0 ,
  input  \Seleçao1 ,
  output Saida
);

  wire mips_mux2_1_saida, mips_mux2_2_saida;

  mips_mux2 mips_mux2_1 (.Entrada0(Entrada0), .Entrada1(Entrada1), .\Seleção (\Seleção0 ), .Saida(mips_mux2_1_saida));
  mips_mux2 mips_mux2_2 (.Entrada0(Entrada2), .Entrada1(Entrada3), .\Seleção (\Seleção0 ), .Saida(mips_mux2_2_saida));
  mips_mux2 mips_mux2_3 (
    .Entrada0(mips_mux2_1_saida), .Entrada1(mips_mux2_2_saida), .\Seleção (\Seleçao1 ), .Saida(Saida));
endmodule
