// Digital circuit mips_mux4_new_32bits.dig as structural Verilog
module mips_mux4_new_32bits (
  input  [31:0] Entrada0,
  input  [31:0] Entrada1,
  input  [31:0] Entrada2,
  input  [31:0] Entrada3,
  input  \Seleção0 ,
  input  \Seleção1 ,
  output [31:0] Saida
);

  wire [31:0] mips_mux2_32bits_1_saida, mips_mux2_32bits_2_saida;

  mips_mux2_32bits mips_mux2_32bits_1 (
    .Entrada0(Entrada0), .Entrada1(Entrada1), .\Seleção (\Seleção0 ), .Saida(mips_mux2_32bits_1_saida));
  mips_mux2_32bits mips_mux2_32bits_2 (
    .Entrada0(Entrada2), .Entrada1(Entrada3), .\Seleção (\Seleção0 ), .Saida(mips_mux2_32bits_2_saida));
  mips_mux2_32bits mips_mux2_32bits_3 (
    .Entrada0(mips_mux2_32bits_1_saida), .Entrada1(mips_mux2_32bits_2_saida), .\Seleção (\Seleção1 ),
    .Saida(Saida));
endmodule
