// Digital circuit mips_regleitura.dig as structural Verilog
module mips_regleitura (
  input  [31:0] Entrada,
  input  Clock,
  output [31:0] Saida
);

  mips_flipflopD mips_flipflopd_1 (.Clock(Clock), .D(Entrada[0]), .Q(Saida[0]));  // open: nQ
  mips_flipflopD mips_flipflopd_2 (.Clock(Clock), .D(Entrada[1]), .Q(Saida[1]));  // open: nQ
  mips_flipflopD mips_flipflopd_3 (.Clock(Clock), .D(Entrada[2]), .Q(Saida[2]));  // open: nQ
  mips_flipflopD mips_flipflopd_4 (.Clock(Clock), .D(Entrada[3]), .Q(Saida[3]));  // open: nQ
  mips_flipflopD mips_flipflopd_5 (.Clock(Clock), .D(Entrada[4]), .Q(Saida[4]));  // open: nQ
  mips_flipflopD mips_flipflopd_6 (.Clock(Clock), .D(Entrada[5]), .Q(Saida[5]));  // open: nQ
  mips_flipflopD mips_flipflopd_7 (.Clock(Clock), .D(Entrada[6]), .Q(Saida[6]));  // open: nQ
  mips_flipflopD mips_flipflopd_8 (.Clock(Clock), .D(Entrada[7]), .Q(Saida[7]));  // open: nQ
  mips_flipflopD mips_flipflopd_9 (.Clock(Clock), .D(Entrada[8]), .Q(Saida[8]));  // open: nQ
  mips_flipflopD mips_flipflopd_10 (.Clock(Clock), .D(Entrada[9]), .Q(Saida[9]));  // open: nQ
  mips_flipflopD mips_flipflopd_11 (.Clock(Clock), .D(Entrada[10]), .Q(Saida[10]));  // open: nQ
  mips_flipflopD mips_flipflopd_12 (.Clock(Clock), .D(Entrada[11]), .Q(Saida[11]));  // open: nQ
  mips_flipflopD mips_flipflopd_13 (.Clock(Clock), .D(Entrada[12]), .Q(Saida[12]));  // open: nQ
  mips_flipflopD mips_flipflopd_14 (.Clock(Clock), .D(Entrada[13]), .Q(Saida[13]));  // open: nQ
  mips_flipflopD mips_flipflopd_15 (.Clock(Clock), .D(Entrada[14]), .Q(Saida[14]));  // open: nQ
  mips_flipflopD mips_flipflopd_16 (.Clock(Clock), .D(Entrada[15]), .Q(Saida[15]));  // open: nQ
  mips_flipflopD mips_flipflopd_17 (.Clock(Clock), .D(Entrada[16]), .Q(Saida[16]));  // open: nQ
  mips_flipflopD mips_flipflopd_18 (.Clock(Clock), .D(Entrada[17]), .Q(Saida[17]));  // open: nQ
  mips_flipflopD mips_flipflopd_19 (.Clock(Clock), .D(Entrada[18]), .Q(Saida[18]));  // open: nQ
  mips_flipflopD mips_flipflopd_20 (.Clock(Clock), .D(Entrada[19]), .Q(Saida[19]));  // open: nQ
  mips_flipflopD mips_flipflopd_21 (.Clock(Clock), .D(Entrada[20]), .Q(Saida[20]));  // open: nQ
  mips_flipflopD mips_flipflopd_22 (.Clock(Clock), .D(Entrada[21]), .Q(Saida[21]));  // open: nQ
  mips_flipflopD mips_flipflopd_23 (.Clock(Clock), .D(Entrada[22]), .Q(Saida[22]));  // open: nQ
  mips_flipflopD mips_flipflopd_24 (.Clock(Clock), .D(Entrada[23]), .Q(Saida[23]));  // open: nQ
  mips_flipflopD mips_flipflopd_25 (.Clock(Clock), .D(Entrada[24]), .Q(Saida[24]));  // open: nQ
  mips_flipflopD mips_flipflopd_26 (.Clock(Clock), .D(Entrada[25]), .Q(Saida[25]));  // open: nQ
  mips_flipflopD mips_flipflopd_27 (.Clock(Clock), .D(Entrada[26]), .Q(Saida[26]));  // open: nQ
  mips_flipflopD mips_flipflopd_28 (.Clock(Clock), .D(Entrada[27]), .Q(Saida[27]));  // open: nQ
  mips_flipflopD mips_flipflopd_29 (.Clock(Clock), .D(Entrada[28]), .Q(Saida[28]));  // open: nQ
  mips_flipflopD mips_flipflopd_30 (.Clock(Clock), .D(Entrada[29]), .Q(Saida[29]));  // open: nQ
  mips_flipflopD mips_flipflopd_31 (.Clock(Clock), .D(Entrada[30]), .Q(Saida[30]));  // open: nQ
  mips_flipflopD mips_flipflopd_32 (.Clock(Clock), .D(Entrada[31]), .Q(Saida[31]));  // open: nQ
endmodule
