// Digital circuit mips_sdram4p2.dig as structural Verilog
module mips_sdram4p2 (
  input  Din,
  input  \Din² ,
  input  [1:0] Entrada,
  input  Write_Enable,
  output Dout,
  output \Dout² 
);

  wire and_1_out, and_2_out, and_3_out, and_4_out, mips_decodificador2entradas_errado_1_saida0,
       mips_decodificador2entradas_errado_1_saida1, mips_decodificador2entradas_errado_1_saida2,
       mips_decodificador2entradas_errado_1_saida3;

  mips_decodificador2entradas_errado mips_decodificador2entradas_errado_1 (
    .Entrada0(Entrada[0]), .Entrada1(Entrada[1]), .Saida0(mips_decodificador2entradas_errado_1_saida0),
    .Saida1(mips_decodificador2entradas_errado_1_saida1),
    .Saida2(mips_decodificador2entradas_errado_1_saida2), .Saida3(mips_decodificador2entradas_errado_1_saida3));
  and and_1 (and_1_out, mips_decodificador2entradas_errado_1_saida0, Write_Enable);
  and and_2 (and_2_out, mips_decodificador2entradas_errado_1_saida1, Write_Enable);
  and and_3 (and_3_out, mips_decodificador2entradas_errado_1_saida2, Write_Enable);
  and and_4 (and_4_out, mips_decodificador2entradas_errado_1_saida3, Write_Enable);
  mips_latchD_enable mips_latchd_enable_1 (.Clock(and_1_out), .D(Din), .Q(Dout));  // open: Enable, nQ
  mips_latchD_enable mips_latchd_enable_2 (.Clock(and_2_out), .D(Din), .Q(Dout));  // open: Enable, nQ
  mips_latchD_enable mips_latchd_enable_3 (.Clock(and_3_out), .D(Din), .Q(Dout));  // open: Enable, nQ
  mips_latchD_enable mips_latchd_enable_4 (.Clock(and_4_out), .D(Din), .Q(Dout));  // open: Enable, nQ
  mips_latchD_enable mips_latchd_enable_5 (
    .Clock(and_1_out), .D(\Din² ), .Enable(mips_decodificador2entradas_errado_1_saida0), .Q(\Dout² ));  // open: nQ
  mips_latchD_enable mips_latchd_enable_6 (
    .Clock(and_2_out), .D(\Din² ), .Enable(mips_decodificador2entradas_errado_1_saida1), .Q(\Dout² ));  // open: nQ
  mips_latchD_enable mips_latchd_enable_7 (
    .Clock(and_3_out), .D(\Din² ), .Enable(mips_decodificador2entradas_errado_1_saida2), .Q(\Dout² ));  // open: nQ
  mips_latchD_enable mips_latchd_enable_8 (
    .Clock(and_4_out), .D(\Din² ), .Enable(mips_decodificador2entradas_errado_1_saida3), .Q(\Dout² ));  // open: nQ
endmodule
