// Digital circuit mips_somador32bits.dig as structural Verilog
module mips_somador32bits (
  input  [31:0] A,
  input  [31:0] B,
  input  Cin,
  output \Saída_0 ,
  output \Saída_1 ,
  output \Saída_2 ,
  output \Saída_3 ,
  output \Saída_4 ,
  output \Saída_5 ,
  output \Saída_6 ,
  output \Saída_7 ,
  output \Saída_8 ,
  output \Saída_9 ,
  output \Saída_10 ,
  output \Saída_11 ,
  output \Saída_12 ,
  output \Saída_13 ,
  output \Saída_14 ,
  output \Saída_15 ,
  output \Saída_16 ,
  output \Saída_17 ,
  output \Saída_18 ,
  output \Saída_19 ,
  output \Saída_20 ,
  output \Saída_21 ,
  output \Saída_22 ,
  output \Saída_23 ,
  output \Saída_24 ,
  output \Saída_25 ,
  output \Saída_26 ,
  output \Saída_27 ,
  output \Saída_28 ,
  output \Saída_29 ,
  output \Saída_30 ,
  output \Saída_31 ,
  output Cout
);

  wire mips_somacomplet_1_carryout, mips_somacomplet_2_carryout, mips_somacomplet_3_carryout,
       mips_somacomplet_4_carryout, mips_somacomplet_5_carryout, mips_somacomplet_6_carryout,
       mips_somacomplet_7_carryout, mips_somacomplet_8_carryout, mips_somacomplet_9_carryout,
       mips_somacomplet_10_carryout, mips_somacomplet_11_carryout, mips_somacomplet_12_carryout,
       mips_somacomplet_13_carryout, mips_somacomplet_14_carryout, mips_somacomplet_15_carryout,
       mips_somacomplet_16_carryout, mips_somacomplet_17_carryout, mips_somacomplet_18_carryout,
       mips_somacomplet_19_carryout, mips_somacomplet_20_carryout, mips_somacomplet_21_carryout,
       mips_somacomplet_22_carryout, mips_somacomplet_23_carryout, mips_somacomplet_24_carryout,
       mips_somacomplet_25_carryout, mips_somacomplet_26_carryout, mips_somacomplet_27_carryout,
       mips_somacomplet_28_carryout, mips_somacomplet_29_carryout, mips_somacomplet_30_carryout,
       mips_somacomplet_31_carryout;

  mips_somacomplet mips_somacomplet_1 (
    .A(A[0]), .B(B[0]), .CarryIn(Cin), .S(\Saída_0 ), .CarryOut(mips_somacomplet_1_carryout));
  mips_somacomplet mips_somacomplet_2 (
    .A(A[1]), .B(B[1]), .CarryIn(mips_somacomplet_1_carryout), .S(\Saída_1 ),
    .CarryOut(mips_somacomplet_2_carryout));
  mips_somacomplet mips_somacomplet_3 (
    .A(A[2]), .B(B[2]), .CarryIn(mips_somacomplet_2_carryout), .S(\Saída_2 ),
    .CarryOut(mips_somacomplet_3_carryout));
  mips_somacomplet mips_somacomplet_4 (
    .A(A[3]), .B(B[3]), .CarryIn(mips_somacomplet_3_carryout), .S(\Saída_3 ),
    .CarryOut(mips_somacomplet_4_carryout));
  mips_somacomplet mips_somacomplet_5 (
    .A(A[4]), .B(B[4]), .CarryIn(mips_somacomplet_4_carryout), .S(\Saída_4 ),
    .CarryOut(mips_somacomplet_5_carryout));
  mips_somacomplet mips_somacomplet_6 (
    .A(A[5]), .B(B[5]), .CarryIn(mips_somacomplet_5_carryout), .S(\Saída_5 ),
    .CarryOut(mips_somacomplet_6_carryout));
  mips_somacomplet mips_somacomplet_7 (
    .A(A[6]), .B(B[6]), .CarryIn(mips_somacomplet_6_carryout), .S(\Saída_6 ),
    .CarryOut(mips_somacomplet_7_carryout));
  mips_somacomplet mips_somacomplet_8 (
    .A(A[7]), .B(B[7]), .CarryIn(mips_somacomplet_7_carryout), .S(\Saída_7 ),
    .CarryOut(mips_somacomplet_8_carryout));
  mips_somacomplet mips_somacomplet_9 (
    .A(A[8]), .B(B[8]), .CarryIn(mips_somacomplet_8_carryout), .S(\Saída_8 ),
    .CarryOut(mips_somacomplet_9_carryout));
  mips_somacomplet mips_somacomplet_10 (
    .A(A[9]), .B(B[9]), .CarryIn(mips_somacomplet_9_carryout), .S(\Saída_9 ),
    .CarryOut(mips_somacomplet_10_carryout));
  mips_somacomplet mips_somacomplet_11 (
    .A(A[10]), .B(B[10]), .CarryIn(mips_somacomplet_10_carryout), .S(\Saída_10 ),
    .CarryOut(mips_somacomplet_11_carryout));
  mips_somacomplet mips_somacomplet_12 (
    .A(A[11]), .B(B[11]), .CarryIn(mips_somacomplet_11_carryout), .S(\Saída_11 ),
    .CarryOut(mips_somacomplet_12_carryout));
  mips_somacomplet mips_somacomplet_13 (
    .A(A[12]), .B(B[12]), .CarryIn(mips_somacomplet_12_carryout), .S(\Saída_12 ),
    .CarryOut(mips_somacomplet_13_carryout));
  mips_somacomplet mips_somacomplet_14 (
    .A(A[13]), .B(B[13]), .CarryIn(mips_somacomplet_13_carryout), .S(\Saída_13 ),
    .CarryOut(mips_somacomplet_14_carryout));
  mips_somacomplet mips_somacomplet_15 (
    .A(A[14]), .B(B[14]), .CarryIn(mips_somacomplet_14_carryout), .S(\Saída_14 ),
    .CarryOut(mips_somacomplet_15_carryout));
  mips_somacomplet mips_somacomplet_16 (
    .A(A[15]), .B(B[15]), .CarryIn(mips_somacomplet_15_carryout), .S(\Saída_15 ),
    .CarryOut(mips_somacomplet_16_carryout));
  mips_somacomplet mips_somacomplet_17 (
    .A(A[16]), .B(B[16]), .CarryIn(mips_somacomplet_16_carryout), .S(\Saída_16 ),
    .CarryOut(mips_somacomplet_17_carryout));
  mips_somacomplet mips_somacomplet_18 (
    .A(A[17]), .B(B[17]), .CarryIn(mips_somacomplet_17_carryout), .S(\Saída_17 ),
    .CarryOut(mips_somacomplet_18_carryout));
  mips_somacomplet mips_somacomplet_19 (
    .A(A[18]), .B(B[18]), .CarryIn(mips_somacomplet_18_carryout), .S(\Saída_18 ),
    .CarryOut(mips_somacomplet_19_carryout));
  mips_somacomplet mips_somacomplet_20 (
    .A(A[19]), .B(B[19]), .CarryIn(mips_somacomplet_19_carryout), .S(\Saída_19 ),
    .CarryOut(mips_somacomplet_20_carryout));
  mips_somacomplet mips_somacomplet_21 (
    .A(A[20]), .B(B[20]), .CarryIn(mips_somacomplet_20_carryout), .S(\Saída_20 ),
    .CarryOut(mips_somacomplet_21_carryout));
  mips_somacomplet mips_somacomplet_22 (
    .A(A[21]), .B(B[21]), .CarryIn(mips_somacomplet_21_carryout), .S(\Saída_21 ),
    .CarryOut(mips_somacomplet_22_carryout));
  mips_somacomplet mips_somacomplet_23 (
    .A(A[22]), .B(B[22]), .CarryIn(mips_somacomplet_22_carryout), .S(\Saída_22 ),
    .CarryOut(mips_somacomplet_23_carryout));
  mips_somacomplet mips_somacomplet_24 (
    .A(A[23]), .B(B[23]), .CarryIn(mips_somacomplet_23_carryout), .S(\Saída_23 ),
    .CarryOut(mips_somacomplet_24_carryout));
  mips_somacomplet mips_somacomplet_25 (
    .A(A[24]), .B(B[24]), .CarryIn(mips_somacomplet_24_carryout), .S(\Saída_24 ),
    .CarryOut(mips_somacomplet_25_carryout));
  mips_somacomplet mips_somacomplet_26 (
    .A(A[25]), .B(B[25]), .CarryIn(mips_somacomplet_25_carryout), .S(\Saída_25 ),
    .CarryOut(mips_somacomplet_26_carryout));
  mips_somacomplet mips_somacomplet_27 (
    .A(A[26]), .B(B[26]), .CarryIn(mips_somacomplet_26_carryout), .S(\Saída_26 ),
    .CarryOut(mips_somacomplet_27_carryout));
  mips_somacomplet mips_somacomplet_28 (
    .A(A[27]), .B(B[27]), .CarryIn(mips_somacomplet_27_carryout), .S(\Saída_27 ),
    .CarryOut(mips_somacomplet_28_carryout));
  mips_somacomplet mips_somacomplet_29 (
    .A(A[28]), .B(B[28]), .CarryIn(mips_somacomplet_28_carryout), .S(\Saída_28 ),
    .CarryOut(mips_somacomplet_29_carryout));
  mips_somacomplet mips_somacomplet_30 (
    .A(A[29]), .B(B[29]), .CarryIn(mips_somacomplet_29_carryout), .S(\Saída_29 ),
    .CarryOut(mips_somacomplet_30_carryout));
  mips_somacomplet mips_somacomplet_31 (
    .A(A[30]), .B(B[30]), .CarryIn(mips_somacomplet_30_carryout), .S(\Saída_30 ),
    .CarryOut(mips_somacomplet_31_carryout));
  mips_somacomplet mips_somacomplet_32 (
    .A(A[31]), .B(B[31]), .CarryIn(mips_somacomplet_31_carryout), .S(\Saída_31 ), .CarryOut(Cout));
endmodule
