// Digital circuit ula32_teste.dig as structural Verilog
module ula32_teste (
  input  Binvert,
  input  Ainvert,
  input  CarryIn,
  input  [1:0] \Operação ,
  input  [31:0] A,
  input  [31:0] B,
  output Result0,
  output Result1,
  output Result2,
  output Result3,
  output Result4,
  output Result5,
  output Result6,
  output Result7,
  output Result8,
  output Result9,
  output Result10,
  output Result11,
  output Result12,
  output Result13,
  output Result14,
  output Result15,
  output Result16,
  output Result17,
  output Result18,
  output Result19,
  output Result20,
  output Result21,
  output Result22,
  output Result23,
  output Result24,
  output Result25,
  output Result26,
  output Result27,
  output Result28,
  output Result29,
  output Result30,
  output Result31,
  output CarryOut,
  output Set
);

  wire ula16bits_teste_1_carryout, ula16bits_teste_2_set;

  ULA16BITS_TESTE ula16bits_teste_1 (
    .Binvert(Binvert), .Ainvert(Ainvert), .CarryIn(CarryIn), .\Operação (\Operação ),
    .Less(ula16bits_teste_2_set), .A(A[15:0]), .B(B[15:0]), .Saida0(Result0), .Saida1(Result1),
    .Saida2(Result2), .Saida3(Result3), .Saida4(Result4), .Saida5(Result5), .Saida6(Result6),
    .Saida7(Result7), .Saida8(Result8), .Saida9(Result9), .Saida10(Result10), .Saida11(Result11),
    .Saida12(Result12), .Saida13(Result13), .Saida14(Result14), .Saida15(Result15),
    .CarryOut(ula16bits_teste_1_carryout), .Set(Set));
  ULA16BITS_TESTE ula16bits_teste_2 (
    .Binvert(Binvert), .Ainvert(Ainvert), .CarryIn(ula16bits_teste_1_carryout), .\Operação (\Operação ),
    .Less(1'b0), .A(A[31:16]), .B(B[31:16]), .Saida0(Result16), .Saida1(Result17), .Saida2(Result18),
    .Saida3(Result19), .Saida4(Result20), .Saida5(Result21), .Saida6(Result22), .Saida7(Result23),
    .Saida8(Result24), .Saida9(Result25), .Saida10(Result26), .Saida11(Result27), .Saida12(Result28),
    .Saida13(Result29), .Saida14(Result30), .Saida15(Result31), .CarryOut(CarryOut),
    .Set(ula16bits_teste_2_set));
endmodule

/* Test case:
	Operação	A	B	Ainvert		Binvert		CarryIn		Result31	Result30	Result29	Result28	Result27	Result26	Result25	Result24	Result23	Result22	Result21	Result20	Result19	Result18	Result17	Result16	Result15	Result14	Result13	Result12	Result11	Result10	Result9		Result8		Result7		Result6		Result5		Result4		Result3		Result2		Result1		Result0
loop(a,32)
	loop(b,32)
		0	(a)	(b)	0	0	0	bits(32,a&b)
		1	(a)	(b)	0	0	0	bits(32,a|b)
		10	(a)	(b)	0	0	0	bits(32,a+b)
		10	(a)	(b)	0	1	1	bits(32,a-b)
		10	(a)	(b)	0	1	0	bits(32,(a-b)<0)
		0	(a)	(b)	1	1	0	bits(32,~(a|b))
	end loop
end loop
*/
